// Logisim project coin.circ as structural Verilog: 4 circuits, main circuit main
module main (
  input  [1:0] in_1,
  input  in_2,
  output [3:0] out_3,
  output out_4
);

  // counter counter_1: pin names not known; wires that end beside it: in_1, in_2, out_3, out_4
endmodule

module counter (
  input  [1:0] in,
  input  in_2,
  output out_3,
  output out_4,
  output out_5,
  output dispense
);

  wire clock_1_out, comparator_1_eq, comparator_1_gt;
  wire [2:0] bit_extender_1_out;
  wire [3:0] multiplexer_1_out, register_1_q, state_1_coin02, subtractor_1_out;

  state state_1 (
    .in1(in[1]), .in0(in[0]), .coin3(register_1_q[3]), .coin2(register_1_q[2]), .coin1(register_1_q[1]),
    .coin0(register_1_q[0]), .coin32(state_1_coin02[3]), .coin22(state_1_coin02[2]),
    .coin12(state_1_coin02[1]), .coin02(state_1_coin02[0]));
  Register #(.width(4)) register_1 (.D(state_1_coin02), .Q(register_1_q), .clk(clock_1_out), .clr(in_2));  // open: en
  Clock clock_1 (.out(clock_1_out));
  Subtractor #(.width(4)) subtractor_1 (.a(register_1_q), .b(4'b0101), .out(subtractor_1_out));  // open: bin, bout
  Comparator #(.width(4), .mode("unsigned")) comparator_1 (
    .a(register_1_q), .b(4'b0101), .gt(comparator_1_gt), .eq(comparator_1_eq));  // open: lt
  Multiplexer #(.width(4), .enable("false")) multiplexer_1 (
    .in0(4'b0000), .in1(subtractor_1_out), .out(multiplexer_1_out), .sel(dispense));
  or or_1 (dispense, comparator_1_gt, comparator_1_eq);
  Bit_Extender #(.in_width(4), .out_width(3)) bit_extender_1 (.in(multiplexer_1_out), .out(bit_extender_1_out));
  find find_1 (
    .in2(bit_extender_1_out[0]), .in1(bit_extender_1_out[1]), .in0(bit_extender_1_out[2]), .out4(out_3),
    .out2(out_4), .out1(out_5));
endmodule

module state (
  input  in1,
  input  in0,
  input  coin3,
  input  coin2,
  input  coin1,
  input  coin0,
  output coin32,
  output coin22,
  output coin12,
  output coin02
);

  wire and_1_out, and_2_out, and_3_out, and_4_out, and_5_out, and_6_out, and_7_out, and_8_out, and_9_out,
       and_10_out, and_11_out, and_12_out, and_13_out, and_14_out, and_15_out, and_16_out, and_17_out,
       and_18_out, and_19_out, and_20_out, and_21_out, not_1_out, not_2_out, not_3_out, not_4_out, not_5_out,
       not_6_out, not_7_out, not_8_out, not_9_out, not_10_out, not_11_out, not_12_out, not_13_out,
       not_14_out, not_15_out, not_16_out, not_17_out, not_18_out, not_19_out, not_20_out, not_21_out,
       not_22_out, not_23_out, not_24_out, not_25_out, not_26_out, not_27_out, not_28_out, not_29_out,
       not_30_out, not_31_out, not_32_out, not_33_out, not_34_out, not_35_out, not_36_out, not_37_out,
       not_38_out, not_39_out, not_40_out, not_41_out, not_42_out;

  not not_1 (not_1_out, coin3);
  not not_2 (not_2_out, coin2);
  not not_3 (not_3_out, coin3);
  not not_4 (not_4_out, coin1);
  not not_5 (not_5_out, coin0);
  not not_6 (not_6_out, in1);
  not not_7 (not_7_out, coin3);
  not not_8 (not_8_out, coin1);
  not not_9 (not_9_out, coin0);
  not not_10 (not_10_out, in0);
  not not_11 (not_11_out, coin3);
  not not_12 (not_12_out, coin1);
  not not_13 (not_13_out, coin0);
  not not_14 (not_14_out, in1);
  not not_15 (not_15_out, coin3);
  not not_16 (not_16_out, coin2);
  not not_17 (not_17_out, in0);
  not not_18 (not_18_out, coin3);
  not not_19 (not_19_out, coin2);
  not not_20 (not_20_out, coin2);
  not not_21 (not_21_out, coin1);
  not not_22 (not_22_out, coin0);
  not not_23 (not_23_out, in1);
  not not_24 (not_24_out, in0);
  not not_25 (not_25_out, coin3);
  not not_26 (not_26_out, coin2);
  not not_27 (not_27_out, coin3);
  not not_28 (not_28_out, coin2);
  not not_29 (not_29_out, coin1);
  not not_30 (not_30_out, coin3);
  not not_31 (not_31_out, coin2);
  not not_32 (not_32_out, coin0);
  not not_33 (not_33_out, in0);
  not not_34 (not_34_out, coin1);
  not not_35 (not_35_out, in0);
  not not_36 (not_36_out, in0);
  not not_37 (not_37_out, in0);
  not not_38 (not_38_out, coin3);
  not not_39 (not_39_out, coin2);
  not not_40 (not_40_out, in1);
  not not_41 (not_41_out, coin1);
  not not_42 (not_42_out, coin0);
  and and_1 (and_1_out, in1, in0, not_1_out, not_2_out, coin1, coin0);
  and and_2 (and_2_out, in1, in0, not_3_out, coin2, not_4_out, not_5_out);
  and and_3 (and_3_out, not_6_out, not_7_out, coin2, not_8_out, not_9_out);
  and and_4 (and_4_out, not_10_out, not_11_out, coin2, not_12_out, not_13_out);
  and and_5 (and_5_out, not_14_out, in0, not_15_out, not_16_out, coin1, coin0);
  and and_6 (and_6_out, in1, not_17_out, not_18_out, not_19_out, coin1);
  and and_7 (and_7_out, in1, in0, not_20_out, not_21_out);
  and and_8 (and_8_out, in1, in0, coin1, not_22_out);
  and and_9 (and_9_out, in1, in0, coin2, coin0);
  and and_10 (and_10_out, in1, in0, coin3);
  and and_11 (and_11_out, not_23_out, not_24_out, not_25_out, not_26_out, coin1);
  and and_12 (and_12_out, in0, not_27_out, not_28_out, not_29_out, coin0);
  and and_13 (and_13_out, in0, not_30_out, not_31_out, coin1, not_32_out);
  and and_14 (and_14_out, in1, not_33_out, not_34_out);
  and and_15 (and_15_out, in1, not_35_out, coin2);
  and and_16 (and_16_out, in1, not_36_out, coin3);
  and and_17 (and_17_out, not_37_out, not_38_out, not_39_out, coin0);
  and and_18 (and_18_out, not_40_out, coin3, coin2, not_41_out, coin0);
  and and_19 (and_19_out, in0, not_42_out);
  and and_20 (and_20_out, in0, coin2);
  and and_21 (and_21_out, in0, coin3);
  or or_1 (coin32, and_1_out, and_2_out);
  or or_2 (coin22, and_3_out, and_4_out, and_5_out, and_6_out, and_7_out, and_8_out, and_9_out, and_10_out);
  or or_3 (coin12, and_11_out, and_12_out, and_13_out, and_14_out, and_15_out, and_16_out);
  or or_4 (coin02, and_17_out, and_18_out, and_19_out, and_20_out, and_21_out);
endmodule

module find (
  input  in2,
  input  in1,
  input  in0,
  output out4,
  output out2,
  output out1
);


  assign out1 = in0;
  assign out2 = in1;
  assign out4 = in2;
endmodule
