// Logisim project sra.circ as structural Verilog: 1 circuit, main circuit main
module main (
  input  [15:0] in_1,
  input  [3:0] in_2,
  output [15:0] out_3
);

  wire [15:0] demultiplexer_1_out0, demultiplexer_1_out1, demultiplexer_2_out0, demultiplexer_2_out1,
       demultiplexer_3_out0, demultiplexer_3_out1, demultiplexer_4_out0, demultiplexer_4_out1, or_1_out,
       or_2_out, or_3_out;

  Demultiplexer #(.width(16), .enable("false")) demultiplexer_1 (
    .out0(demultiplexer_1_out0), .out1(demultiplexer_1_out1), .in(in_1), .sel(in_2[0]));
  Demultiplexer #(.width(16), .enable("false")) demultiplexer_2 (
    .out0(demultiplexer_2_out0), .out1(demultiplexer_2_out1), .in(or_1_out), .sel(in_2[1]));
  assign or_1_out = demultiplexer_1_out0 | {{2{demultiplexer_1_out1[15]}}, demultiplexer_1_out1[14:1]};  // OR_Gate or_1, 16 bits wide
  Demultiplexer #(.width(16), .enable("false")) demultiplexer_3 (
    .out0(demultiplexer_3_out0), .out1(demultiplexer_3_out1), .in(or_2_out), .sel(in_2[2]));
  assign or_2_out = demultiplexer_2_out0 | {{3{demultiplexer_2_out1[15]}}, demultiplexer_2_out1[14:2]};  // OR_Gate or_2, 16 bits wide
  Demultiplexer #(.width(16), .enable("false")) demultiplexer_4 (
    .out0(demultiplexer_4_out0), .out1(demultiplexer_4_out1), .in(or_3_out), .sel(in_2[3]));
  assign or_3_out = demultiplexer_3_out0 | {{5{demultiplexer_3_out1[15]}}, demultiplexer_3_out1[14:4]};  // OR_Gate or_3, 16 bits wide
  assign out_3 = {{9{demultiplexer_4_out1[15]}}, demultiplexer_4_out1[14:8]} | demultiplexer_4_out0;  // OR_Gate or_4, 16 bits wide
endmodule
