// Logisim project CRC.circ as structural Verilog: 3 circuits, main circuit main
module main (
  input  [7:0] A,
  input  [3:0] B,
  output [10:0] out_3
);

  CRC crc_1 (.A(A), .B(B), .out_3(out_3));
endmodule

module _4bit_div (
  input  [3:0] A,
  input  [3:0] B,
  output div,
  output [2:0] rem
);

  wire bitselector_1_out, bitselector_2_out;
  wire [3:0] multiplexer_1_out, xor_1_out;

  BitSelector #(.width(4)) bitselector_1 (.in(A), .out(bitselector_1_out), .sel(2'b11));
  BitSelector #(.width(4)) bitselector_2 (.in(B), .out(bitselector_2_out), .sel(2'b11));
  and and_1 (div, bitselector_1_out, bitselector_2_out);
  assign xor_1_out = A ^ B;  // XOR_Gate xor_1, 4 bits wide
  Multiplexer #(.width(4), .enable("false")) multiplexer_1 (
    .in0(A), .in1(xor_1_out), .out(multiplexer_1_out), .sel(div));
  Bit_Extender #(.in_width(4), .out_width(3)) bit_extender_1 (.in(multiplexer_1_out), .out(rem));
endmodule

module CRC (
  input  [7:0] A,
  input  [3:0] B,
  output [10:0] out_3
);

  wire [2:0] n4bit_div_1_rem, n4bit_div_2_rem, n4bit_div_3_rem, n4bit_div_4_rem, n4bit_div_5_rem,
       n4bit_div_6_rem;
  wire [3:1] n4bit_div_7_rem;

  _4bit_div u_4bit_div_1 (.A(A[7:4]), .B(B), .rem(n4bit_div_1_rem));  // open: div
  _4bit_div u_4bit_div_2 (.A({n4bit_div_1_rem, A[3]}), .B(B), .rem(n4bit_div_2_rem));  // open: div
  _4bit_div u_4bit_div_3 (.A({n4bit_div_2_rem, A[2]}), .B(B), .rem(n4bit_div_3_rem));  // open: div
  _4bit_div u_4bit_div_4 (.A({n4bit_div_3_rem, A[1]}), .B(B), .rem(n4bit_div_4_rem));  // open: div
  _4bit_div u_4bit_div_5 (.A({n4bit_div_4_rem, A[0]}), .B(B), .rem(n4bit_div_5_rem));  // open: div
  _4bit_div u_4bit_div_6 (.A({n4bit_div_5_rem, 1'b0}), .B(B), .rem(n4bit_div_6_rem));  // open: div
  _4bit_div u_4bit_div_7 (.A({n4bit_div_6_rem, 1'b0}), .B(B), .rem(n4bit_div_7_rem));  // open: div
  _4bit_div u_4bit_div_8 (.A({n4bit_div_7_rem, 1'b0}), .B(B), .rem(out_3[2:0]));  // open: div

  assign out_3[10:3] = A;
endmodule
