// Logisim project fsm.circ as structural Verilog: 3 circuits, main circuit main
module main (
  input  clr,
  input  [1:0] In,
  output out_3
);

  fsm fsm_1 (.clr(clr), .In(In), .z(out_3));
endmodule

module fsm (
  input  clr,
  input  [1:0] In,
  output z
);

  wire clock_1_out, decoder_1_out1, decoder_2_out0, decoder_2_out2, decoder_3_out0, decoder_3_out2, or_1_out,
       or_2_out;
  wire [1:0] shift_register_1_q0, shift_register_1_q1;

  Shift_Register #(.width(2), .length(2)) shift_register_1 (
    .in(In), .clk(clock_1_out), .load(clr), .d0(2'b00), .q0(shift_register_1_q0), .d1(2'b00),
    .q1(shift_register_1_q1));  // open: shift, out, clr
  Clock clock_1 (.out(clock_1_out));
  Decoder #(.select(2), .disabled(0), .enable("false")) decoder_1 (
    .out1(decoder_1_out1), .sel(shift_register_1_q1));  // open: out0, out2, out3
  Decoder #(.select(2), .disabled(0), .enable("false")) decoder_2 (
    .out0(decoder_2_out0), .out2(decoder_2_out2), .sel(shift_register_1_q0));  // open: out1, out3
  Decoder #(.select(2), .disabled(0), .enable("false")) decoder_3 (
    .out0(decoder_3_out0), .out2(decoder_3_out2), .sel(In));  // open: out1, out3
  or or_1 (or_1_out, decoder_2_out0, decoder_2_out2);
  or or_2 (or_2_out, decoder_3_out0, decoder_3_out2);
  and and_1 (z, decoder_1_out1, or_1_out, or_2_out);
endmodule

module fsm2 (
  input  clr,
  input  [1:0] In,
  output z
);

  wire clock_1_out, decoder_1_out1, decoder_2_out0, decoder_2_out2, decoder_3_out0, decoder_3_out2, or_1_out,
       or_2_out;
  wire [1:0] multiplexer_1_out, multiplexer_2_out, multiplexer_3_out, register_1_q, register_2_q;

  Clock clock_1 (.out(clock_1_out));
  Multiplexer #(.width(2), .enable("false")) multiplexer_1 (
    .in0(register_2_q), .in1(2'b00), .out(multiplexer_1_out), .sel(clr));
  Multiplexer #(.width(2), .enable("false")) multiplexer_2 (.in0(In), .in1(2'b00), .out(multiplexer_2_out), .sel(clr));
  Multiplexer #(.width(2), .enable("false")) multiplexer_3 (.in0(In), .in1(2'b00), .out(multiplexer_3_out), .sel(clr));
  Register #(.width(2)) register_1 (.D(multiplexer_1_out), .Q(register_1_q), .clk(clock_1_out));  // open: en, clr
  Register #(.width(2)) register_2 (.D(multiplexer_2_out), .Q(register_2_q), .clk(clock_1_out));  // open: en, clr
  Decoder #(.select(2), .disabled(0), .enable("false")) decoder_1 (
    .out1(decoder_1_out1), .sel(register_1_q));  // open: out0, out2, out3
  Decoder #(.select(2), .disabled(0), .enable("false")) decoder_2 (
    .out0(decoder_2_out0), .out2(decoder_2_out2), .sel(register_2_q));  // open: out1, out3
  Decoder #(.select(2), .disabled(0), .enable("false")) decoder_3 (
    .out0(decoder_3_out0), .out2(decoder_3_out2), .sel(multiplexer_3_out));  // open: out1, out3
  or or_1 (or_1_out, decoder_2_out0, decoder_2_out2);
  and and_1 (z, decoder_1_out1, or_1_out, or_2_out);
  or or_2 (or_2_out, decoder_3_out0, decoder_3_out2);
endmodule
