// Logisim project ftoi.circ as structural Verilog
module ftoi (
  input  [15:0] float,
  output [31:0] \int 
);

  wire comparator_1_eq, comparator_2_lt, or_1_out;
  wire [3:0] bit_extender_2_out, subtractor_1_out;
  wire [4:0] Exp;
  wire [15:0] bit_extender_1_out, shifter_1_out, shifter_2_out;
  wire [31:0] bit_extender_3_out, Int_t, negator_1_out;

  // Probe on Exp
  // Probe on float[9:0]
  // Probe on Int_t
  assign bit_extender_1_out = {{5{1'b0}}, {1'b1, float[9:0]}};  // Bit_Extender bit_extender_1
  Bit_Extender #(.in_width(5), .out_width(4)) bit_extender_2 (.in(Exp), .out(bit_extender_2_out));
  // Probe on shifter_1_out
  Shifter #(.width(16)) shifter_1 (.in(bit_extender_1_out), .\dist (4'b0101), .out(shifter_1_out));
  Subtractor #(.width(4)) subtractor_1 (
    .a(4'b1111), .b(bit_extender_2_out), .out(subtractor_1_out));  // open: bin, bout
  // Probe on shifter_2_out
  Shifter #(.width(16), .shift("lr")) shifter_2 (.in(shifter_1_out), .\dist (subtractor_1_out), .out(shifter_2_out));
  assign bit_extender_3_out = {{16{1'b0}}, shifter_2_out};  // Bit_Extender bit_extender_3
  Negator #(.width(32)) negator_1 (.in(bit_extender_3_out), .out(negator_1_out));
  Subtractor #(.width(5)) subtractor_2 (.a(float[14:10]), .b(5'b01111), .out(Exp));  // open: bin, bout
  Multiplexer #(.width(32), .enable("false")) multiplexer_1 (
    .in0(bit_extender_3_out), .in1(negator_1_out), .out(Int_t), .sel(float[15]));
  Comparator #(.width(5), .mode("unsigned")) comparator_1 (
    .a(float[14:10]), .b({5{1'b1}}), .eq(comparator_1_eq));  // open: gt, lt
  or or_1 (or_1_out, comparator_1_eq, comparator_2_lt);
  Comparator #(.width(5)) comparator_2 (.a(Exp), .b({5{1'b0}}), .lt(comparator_2_lt));  // open: gt, eq
  Multiplexer #(.width(32), .enable("false")) multiplexer_2 (
    .in0(Int_t), .in1({32{1'b0}}), .out(\int ), .sel(or_1_out));

  // Other names for the same wires on the sheet: frac[9:0] = float[9:0]; exp_t[4:0] = float[14:10]; Sign = float[15]
endmodule
