// Logisim project grf.circ as structural Verilog: 3 circuits, main circuit main
module main (
  input  WE,
  input  reset,
  input  [4:0] A1,
  input  [4:0] A2,
  input  [4:0] A3,
  input  [31:0] WD,
  output [31:0] out_7,
  output [31:0] out_8
);

  wire clock_1_out;

  Clock clock_1 (.out(clock_1_out));
  grf grf_1 (.A1(A1), .A2(A2), .A3(A3), .WD(WD), .clk(clock_1_out), .reset(reset), .we(WE), .RD1(out_7), .RD2(out_8));
endmodule

module grf (
  input  clk,
  input  reset,
  input  we,
  input  [4:0] A1,
  input  [4:0] A2,
  input  [4:0] A3,
  input  [31:0] WD,
  output [31:0] RD1,
  output [31:0] RD2
);

  wire _00, _0a, _0b, _0c, _0d, _0e, _0f, _01, _1a, _1b, _1c, _1d, _1e, _1f, _02, _03, _04, _05, _06, _07,
       _08, _09, _10, _11, _12, _13, _14, _15, _16, _17, _18, _19;
  wire [31:0] _00_prime, _0a_prime, _0b_prime, _0c_prime, _0d_prime, _0e_prime, _0f_prime, _01_prime,
       _1a_prime, _1b_prime, _1c_prime, _1d_prime, _1e_prime, _1f_prime, _02_prime, _03_prime, _04_prime,
       _05_prime, _06_prime, _07_prime, _08_prime, _09_prime, _10_prime, _11_prime, _12_prime, _13_prime,
       _14_prime, _15_prime, _16_prime, _17_prime, _18_prime, _19_prime;

  Demultiplexer #(.select(5), .enable("false")) demultiplexer_1 (
    .out0(_00), .out1(_01), .out2(_02), .out3(_03), .out4(_04), .out5(_05), .out6(_06), .out7(_07),
    .out8(_08), .out9(_09), .out10(_0a), .out11(_0b), .out12(_0c), .out13(_0d), .out14(_0e), .out15(_0f),
    .out16(_10), .out17(_11), .out18(_12), .out19(_13), .out20(_14), .out21(_15), .out22(_16), .out23(_17),
    .out24(_18), .out25(_19), .out26(_1a), .out27(_1b), .out28(_1c), .out29(_1d), .out30(_1e), .out31(_1f),
    .in(we), .sel(A3));
  Multiplexer #(.select(5), .width(32), .enable("false")) multiplexer_1 (
    .in0(_00_prime), .in1(_01_prime), .in2(_02_prime), .in3(_03_prime), .in4(_04_prime), .in5(_05_prime),
    .in6(_06_prime), .in7(_07_prime), .in8(_08_prime), .in9(_09_prime), .in10(_0a_prime), .in11(_0b_prime),
    .in12(_0c_prime), .in13(_0d_prime), .in14(_0e_prime), .in15(_0f_prime), .in16(_10_prime),
    .in17(_11_prime), .in18(_12_prime), .in19(_13_prime), .in20(_14_prime), .in21(_15_prime),
    .in22(_16_prime), .in23(_17_prime), .in24(_18_prime), .in25(_19_prime), .in26(_1a_prime),
    .in27(_1b_prime), .in28(_1c_prime), .in29(_1d_prime), .in30(_1e_prime), .in31(_1f_prime), .out(RD1),
    .sel(A1));
  Register #(.width(32)) u__00 (.D(WD), .en(1'b0), .Q(_00_prime), .clk(clk), .clr(reset));
  Register #(.width(32)) u__01 (.D(WD), .en(_01), .Q(_01_prime), .clk(clk), .clr(reset));
  Register #(.width(32)) u__02 (.D(WD), .en(_02), .Q(_02_prime), .clk(clk), .clr(reset));
  Register #(.width(32)) u__03 (.D(WD), .en(_03), .Q(_03_prime), .clk(clk), .clr(reset));
  Register #(.width(32)) u__04 (.D(WD), .en(_04), .Q(_04_prime), .clk(clk), .clr(reset));
  Register #(.width(32)) u__05 (.D(WD), .en(_05), .Q(_05_prime), .clk(clk), .clr(reset));
  Register #(.width(32)) u__06 (.D(WD), .en(_06), .Q(_06_prime), .clk(clk), .clr(reset));
  Register #(.width(32)) u__07 (.D(WD), .en(_07), .Q(_07_prime), .clk(clk), .clr(reset));
  Multiplexer #(.select(5), .width(32), .enable("false")) multiplexer_2 (
    .in0(_00_prime), .in1(_01_prime), .in2(_02_prime), .in3(_03_prime), .in4(_04_prime), .in5(_05_prime),
    .in6(_06_prime), .in7(_07_prime), .in8(_08_prime), .in9(_09_prime), .in10(_0a_prime), .in11(_0b_prime),
    .in12(_0c_prime), .in13(_0d_prime), .in14(_0e_prime), .in15(_0f_prime), .in16(_10_prime),
    .in17(_11_prime), .in18(_12_prime), .in19(_13_prime), .in20(_14_prime), .in21(_15_prime),
    .in22(_16_prime), .in23(_17_prime), .in24(_18_prime), .in25(_19_prime), .in26(_1a_prime),
    .in27(_1b_prime), .in28(_1c_prime), .in29(_1d_prime), .in30(_1e_prime), .in31(_1f_prime), .out(RD2),
    .sel(A2));
  Register #(.width(32)) u__08 (.D(WD), .en(_08), .Q(_08_prime), .clk(clk), .clr(reset));
  Register #(.width(32)) u__09 (.D(WD), .en(_09), .Q(_09_prime), .clk(clk), .clr(reset));
  Register #(.width(32)) u__0a (.D(WD), .en(_0a), .Q(_0a_prime), .clk(clk), .clr(reset));
  Register #(.width(32)) u__0b (.D(WD), .en(_0b), .Q(_0b_prime), .clk(clk), .clr(reset));
  Register #(.width(32)) u__0c (.D(WD), .en(_0c), .Q(_0c_prime), .clk(clk), .clr(reset));
  Register #(.width(32)) u__0d (.D(WD), .en(_0d), .Q(_0d_prime), .clk(clk), .clr(reset));
  Register #(.width(32)) u__0e (.D(WD), .en(_0e), .Q(_0e_prime), .clk(clk), .clr(reset));
  Register #(.width(32)) u__0f (.D(WD), .en(_0f), .Q(_0f_prime), .clk(clk), .clr(reset));
  Register #(.width(32)) u__10 (.D(WD), .en(_10), .Q(_10_prime), .clk(clk), .clr(reset));
  Register #(.width(32)) u__11 (.D(WD), .en(_11), .Q(_11_prime), .clk(clk), .clr(reset));
  Register #(.width(32)) u__12 (.D(WD), .en(_12), .Q(_12_prime), .clk(clk), .clr(reset));
  Register #(.width(32)) u__13 (.D(WD), .en(_13), .Q(_13_prime), .clk(clk), .clr(reset));
  Register #(.width(32)) u__14 (.D(WD), .en(_14), .Q(_14_prime), .clk(clk), .clr(reset));
  Register #(.width(32)) u__15 (.D(WD), .en(_15), .Q(_15_prime), .clk(clk), .clr(reset));
  Register #(.width(32)) u__16 (.D(WD), .en(_16), .Q(_16_prime), .clk(clk), .clr(reset));
  Register #(.width(32)) u__17 (.D(WD), .en(_17), .Q(_17_prime), .clk(clk), .clr(reset));
  Register #(.width(32)) u__18 (.D(WD), .en(_18), .Q(_18_prime), .clk(clk), .clr(reset));
  Register #(.width(32)) u__19 (.D(WD), .en(_19), .Q(_19_prime), .clk(clk), .clr(reset));
  Register #(.width(32)) u__1a (.D(WD), .en(_1a), .Q(_1a_prime), .clk(clk), .clr(reset));
  Register #(.width(32)) u__1b (.D(WD), .en(_1b), .Q(_1b_prime), .clk(clk), .clr(reset));
  Register #(.width(32)) u__1c (.D(WD), .en(_1c), .Q(_1c_prime), .clk(clk), .clr(reset));
  Register #(.width(32)) u__1d (.D(WD), .en(_1d), .Q(_1d_prime), .clk(clk), .clr(reset));
  Register #(.width(32)) u__1e (.D(WD), .en(_1e), .Q(_1e_prime), .clk(clk), .clr(reset));
  Register #(.width(32)) u__1f (.D(WD), .en(_1f), .Q(_1f_prime), .clk(clk), .clr(reset));

  // Other names for the same wires on the sheet: data[31:0] = WD
endmodule

module grf2 (
  input  [4:0] A1,
  input  [4:0] A2,
  input  [4:0] A3,
  input  [31:0] WD,
  input  clk,
  input  reset,
  input  we,
  output [31:0] RD1,
  output [31:0] RD2
);

  wire clock_1_out;
  wire [31:0] _00, _00_prime, _0a, _0a_prime, _0b, _0b_prime, _0c, _0c_prime, _0d, _0d_prime, _0e, _0e_prime,
       _0f, _0f_prime, _01, _01_prime, _1a, _1a_prime, _1b, _1b_prime, _1c, _1c_prime, _1d, _1d_prime, _1e,
       _1e_prime, _1f, _1f_prime, _02, _02_prime, _03, _03_prime, _04, _04_prime, _05, _05_prime, _06,
       _06_prime, _07, _07_prime, _08, _08_prime, _09, _09_prime, _10, _10_prime, _11, _11_prime, _12,
       _12_prime, _13, _13_prime, _14, _14_prime, _15, _15_prime, _16, _16_prime, _17, _17_prime, _18,
       _18_prime, _19, _19_prime;

  Demultiplexer #(.select(5), .width(32), .disabled(0)) demultiplexer_1 (
    .out0(_00), .out1(_01), .out2(_02), .out3(_03), .out4(_04), .out5(_05), .out6(_06), .out7(_07),
    .out8(_08), .out9(_09), .out10(_0a), .out11(_0b), .out12(_0c), .out13(_0d), .out14(_0e), .out15(_0f),
    .out16(_10), .out17(_11), .out18(_12), .out19(_13), .out20(_14), .out21(_15), .out22(_16), .out23(_17),
    .out24(_18), .out25(_19), .out26(_1a), .out27(_1b), .out28(_1c), .out29(_1d), .out30(_1e), .out31(_1f),
    .in(WD), .sel(A3), .en(we));
  Clock clock_1 (.out(clock_1_out));
  Shift_Register #(.width(32), .length(32)) shift_register_1 (
    .clk(clock_1_out), .load(clock_1_out), .clr(reset), .d0({32{1'b0}}), .q0(_00_prime), .d1(_01),
    .q1(_01_prime), .d2(_02), .q2(_02_prime), .d3(_03), .q3(_03_prime), .d4(_04), .q4(_04_prime), .d5(_05),
    .q5(_05_prime), .d6(_06), .q6(_06_prime), .d7(_07), .q7(_07_prime), .d8(_08), .q8(_08_prime), .d9(_09),
    .q9(_09_prime), .d10(_0a), .q10(_0a_prime), .d11(_0b), .q11(_0b_prime), .d12(_0c), .q12(_0c_prime),
    .d13(_0d), .q13(_0d_prime), .d14(_0e), .q14(_0e_prime), .d15(_0f), .q15(_0f_prime), .d16(_10),
    .q16(_10_prime), .d17(_11), .q17(_11_prime), .d18(_12), .q18(_12_prime), .d19(_13), .q19(_13_prime),
    .d20(_14), .q20(_14_prime), .d21(_15), .q21(_15_prime), .d22(_16), .q22(_16_prime), .d23(_17),
    .q23(_17_prime), .d24(_18), .q24(_18_prime), .d25(_19), .q25(_19_prime), .d26(_1a), .q26(_1a_prime),
    .d27(_1b), .q27(_1b_prime), .d28(_1c), .q28(_1c_prime), .d29(_1d), .q29(_1d_prime), .d30(_1e),
    .q30(_1e_prime), .d31(_1f), .q31(_1f_prime));  // open: shift, in, out
  Multiplexer #(.select(5), .width(32), .enable("false")) multiplexer_1 (
    .in0(_00_prime), .in1(_01_prime), .in2(_02_prime), .in3(_03_prime), .in4(_04_prime), .in5(_05_prime),
    .in6(_06_prime), .in7(_07_prime), .in8(_08_prime), .in9(_09_prime), .in10(_0a_prime), .in11(_0b_prime),
    .in12(_0c_prime), .in13(_0d_prime), .in14(_0e_prime), .in15(_0f_prime), .in16(_10_prime),
    .in17(_11_prime), .in18(_12_prime), .in19(_13_prime), .in20(_14_prime), .in21(_15_prime),
    .in22(_16_prime), .in23(_17_prime), .in24(_18_prime), .in25(_19_prime), .in26(_1a_prime),
    .in27(_1b_prime), .in28(_1c_prime), .in29(_1d_prime), .in30(_1e_prime), .in31(_1f_prime), .out(RD1),
    .sel(A1));
  Multiplexer #(.select(5), .width(32), .enable("false")) multiplexer_2 (
    .in0(_00_prime), .in1(_01_prime), .in2(_02_prime), .in3(_03_prime), .in4(_04_prime), .in5(_05_prime),
    .in6(_06_prime), .in7(_07_prime), .in8(_08_prime), .in9(_09_prime), .in10(_0a_prime), .in11(_0b_prime),
    .in12(_0c_prime), .in13(_0d_prime), .in14(_0e_prime), .in15(_0f_prime), .in16(_10_prime),
    .in17(_11_prime), .in18(_12_prime), .in19(_13_prime), .in20(_14_prime), .in21(_15_prime),
    .in22(_16_prime), .in23(_17_prime), .in24(_18_prime), .in25(_19_prime), .in26(_1a_prime),
    .in27(_1b_prime), .in28(_1c_prime), .in29(_1d_prime), .in30(_1e_prime), .in31(_1f_prime), .out(RD2),
    .sel(A2));

  // Other names for the same wires on the sheet: data[31:0] = WD
endmodule
