// Logisim project p3-2.circ as structural Verilog: 10 circuits, main circuit main
module main (
  input  in_1,
  output [31:0] out_2,
  output out_3,
  output [4:0] out_4,
  output [31:0] out_5,
  output out_6,
  output [4:0] out_7,
  output [31:0] out_8
);

  wire alu_1_cout, Byte, Clk, comp_1_out_2, comp_1_out_3, comp_1_out_4, controller_1_alusrc,
       controller_1_link, controller_1_memtoreg, controller_1_regdst, controller_1_reglink, Equal_out, Half,
       Jump, Less_out, More_out, Offset, Return, Sign;
  wire [1:0] Ext_Op;
  wire [2:0] controller_1_branch;
  wire [3:0] controller_1_aluctrl;
  wire [4:0] rd, rs, rt, Shamt;
  wire [5:0] Funct, Opcode;
  wire [15:0] decoder_1__16_immediate;
  wire [23:0] bit_extender_1_out, bit_extender_3_out, shifter_3_out;
  wire [25:0] decoder_1__26_immediate, subtractor_1_out;
  wire [31:0] adder_1_out, adder_2_out, adder_3_out, Addr, alu_1_out, bit_extender_2_out, extender_1_out_3,
       grf_1_rd1, grf_1_rd2, memdata_2_out_5, multiplexer_1_out, multiplexer_2_out, multiplexer_3_out,
       ram_1_data, register_1_q, shifter_1_out, subtractor_2_out;

  Clock clock_1 (.out(Clk));
  Shifter #(.width(32)) shifter_1 (.in(adder_2_out), .\dist (5'b00010), .out(shifter_1_out));
  Multiplexer #(.width(32), .enable("false")) multiplexer_1 (
    .in0(adder_2_out), .in1(adder_3_out), .out(multiplexer_1_out), .sel(Offset));
  Register #(.width(32)) register_1 (.D(multiplexer_2_out), .Q(register_1_q), .clk(Clk), .clr(in_1));  // open: en
  Multiplexer #(.width(32), .enable("false")) multiplexer_2 (
    .in0(multiplexer_1_out), .in1(multiplexer_3_out), .out(multiplexer_2_out), .sel(Jump));
  Controller controller_1 (
    .funct(Funct), .RegDst(controller_1_regdst), .ALUSrc(controller_1_alusrc),
    .MemtoReg(controller_1_memtoreg), .RegWrite(out_3), .MemWrite(out_6), .ALUCtrl(controller_1_aluctrl),
    .Ext_Op(Ext_Op), .Branch(controller_1_branch), .Jump(Jump), .Link(controller_1_link), .\return (Return),
    .\byte (Byte), .opcode(Opcode), .half(Half), .RegLink(controller_1_reglink), .Sign(Sign));
  Adder #(.width(32)) adder_1 (.a(shifter_1_out), .b(32'h3000), .out(adder_1_out));  // open: cin, cout
  Adder #(.width(32)) adder_2 (.a(register_1_q), .b(32'h1), .out(adder_2_out));  // open: cin, cout
  Bit_Extender #(.in_width(32), .out_width(24)) bit_extender_1 (.in(register_1_q), .out(bit_extender_1_out));
  ROM #(.addrWidth(24), .dataWidth(32)) rom_1 (.addr(bit_extender_1_out), .data(out_2));  // open: sel
  Decoder decoder_1 (
    .Instr(out_2), .opcode(Opcode), .rs(rs), .rt(rt), .rd(rd), .shamt(Shamt), .funct(Funct),
    ._16_immediate(decoder_1__16_immediate), ._26_immediate(decoder_1__26_immediate));
  assign bit_extender_2_out = {{6{1'b0}}, subtractor_1_out};  // Bit_Extender bit_extender_2
  Subtractor #(.width(26)) subtractor_1 (
    .a(decoder_1__26_immediate), .b(26'hc00), .out(subtractor_1_out));  // open: bin, bout
  grf grf_1 (
    .AluData(alu_1_out), .MemData(memdata_2_out_5), .rs(rs), .rt(rt), .rd(rd), .nPCAddr(adder_1_out),
    .RD1(grf_1_rd1), .RD2(grf_1_rd2), .RegDst(controller_1_regdst), .MemToReg(controller_1_memtoreg),
    .Link(controller_1_link), .clk(Clk), .reset(in_1), .we(out_3), .RegData(out_5), .RegAddr(out_4),
    .RegLink(controller_1_reglink));
  Extender extender_1 (.in_2(decoder_1__16_immediate), .out_3(extender_1_out_3), .in_1(Ext_Op));
  Subtractor #(.width(32)) subtractor_2 (.a(grf_1_rd1), .b(32'h3000), .out(subtractor_2_out));  // open: bin, bout
  Multiplexer #(.width(32), .enable("false")) multiplexer_3 (
    .in0(bit_extender_2_out), .in1(Addr), .out(multiplexer_3_out), .sel(Return));
  Shifter #(.width(32), .shift("lr")) shifter_2 (.in(subtractor_2_out), .\dist (5'b00010), .out(Addr));
  Adder #(.width(32)) adder_3 (.a(extender_1_out_3), .b(adder_2_out), .out(adder_3_out));  // open: cin, cout
  // Probe on alu_1_cout
  ALU alu_1 (
    .in_1(controller_1_aluctrl), .in_2(grf_1_rd1), .in_4(grf_1_rd2), .out(alu_1_out), .cout(alu_1_cout),
    .in_6(Shamt), .in_5(extender_1_out_3), .AluSrc(controller_1_alusrc));
  MemData memdata_1 (.in_4(grf_1_rd2), .Byte(Byte), .Half(Half), .out_5(out_8), .Sign(Sign));
  Bit_Extender #(.in_width(32), .out_width(24)) bit_extender_3 (.in(alu_1_out), .out(bit_extender_3_out));
  Shifter #(.width(24), .shift("lr")) shifter_3 (.in(bit_extender_3_out), .\dist (5'b00010), .out(shifter_3_out));
  Bit_Extender #(.in_width(24), .out_width(5)) bit_extender_4 (.in(shifter_3_out), .out(out_7));
  Comp comp_1 (.in_1(alu_1_out), .out_2(comp_1_out_2), .out_3(comp_1_out_3), .out_4(comp_1_out_4));
  RAM #(.addrWidth(24), .dataWidth(32), .bus("separate")) ram_1 (
    .addr(shifter_3_out), .din(out_8), .data(ram_1_data), .str(out_6), .clk(Clk), .clr(in_1));  // open: sel, ld
  and More (More_out, comp_1_out_2, controller_1_branch[0]);
  and Equal (Equal_out, comp_1_out_3, controller_1_branch[1]);
  and Less (Less_out, comp_1_out_4, controller_1_branch[2]);
  or or_1 (Offset, More_out, Equal_out, Less_out);
  MemData memdata_2 (.in_4(ram_1_data), .Byte(Byte), .Half(Half), .out_5(memdata_2_out_5), .Sign(Sign));

  // Other names for the same wires on the sheet: Instr[31:0] = out_2; MemAddr[4:0] = out_7; MemData[31:0] = out_8;
  //   MemWrite = out_6; RegAddr[4:0] = out_4; RegData[31:0] = out_5; RegWrite = out_3; Reset = in_1

  // Notes on the sheet:
  //   contents of rom_1 (hex, n*v repeats v):
  //   34080000 34090001 1095023 1495021 1148fffe 3c0affff ac0a0000 8c090000 112a0001 12a4821
endmodule

module ALU (
  input  [3:0] in_1,
  input  [31:0] in_2,
  input  AluSrc,
  input  [31:0] in_4,
  input  [31:0] in_5,
  input  [4:0] in_6,
  output [31:0] out,
  output cout
);

  wire bitselector_1_out, bitselector_2_out, bitselector_3_out, bitselector_4_out, nor_1_out,
       signed_cout_minus, signed_cout_plus, unsigned_cout_minus, unsigned_cout_plus, xnor_1_out, xnor_2_out,
       xor_2_out;
  wire [2:0] comparator_1_gt, comparator_2_gt;
  wire [31:0] B, out_and, out_AR, out_LL, out_LR, out_minus, out_mul, out_not, out_or, out_plus, out_xor,
       signed_out_comp, unsigned_out_comp;

  Multiplexer #(.width(32), .enable("false")) multiplexer_1 (.in0(in_4), .in1(in_5), .out(B), .sel(AluSrc));
  Comparator #(.width(32), .mode("unsigned")) comparator_1 (
    .a(in_2), .b(B), .gt(comparator_1_gt[0]), .eq(comparator_1_gt[1]), .lt(comparator_1_gt[2]));
  Comparator #(.width(32)) comparator_2 (
    .a(in_2), .b(B), .gt(comparator_2_gt[0]), .eq(comparator_2_gt[1]), .lt(comparator_2_gt[2]));
  Adder #(.width(32)) adder_1 (.a(in_2), .b(B), .out(out_plus), .cout(unsigned_cout_plus));  // open: cin
  Subtractor #(.width(32)) subtractor_1 (.a(in_2), .b(B), .out(out_minus), .bout(unsigned_cout_minus));  // open: bin
  Shifter #(.width(32)) shifter_1 (.in(B), .\dist (in_6), .out(out_LL));
  Shifter #(.width(32), .shift("lr")) shifter_2 (.in(B), .\dist (in_6), .out(out_LR));
  Shifter #(.width(32), .shift("ar")) shifter_3 (.in(B), .\dist (in_6), .out(out_AR));
  assign out_or = in_2 | B;  // OR_Gate or_1, 32 bits wide
  assign out_and = in_2 & B;  // AND_Gate and_1, 32 bits wide
  assign out_xor = in_2 ^ B;  // XOR_Gate xor_1, 32 bits wide
  assign out_not = ~in_2;  // NOT_Gate not_1, 32 bits wide
  assign unsigned_out_comp = {{29{1'b0}}, comparator_1_gt};  // Bit_Extender bit_extender_1
  assign signed_out_comp = {{29{1'b0}}, comparator_2_gt};  // Bit_Extender bit_extender_2
  Multiplier #(.width(32)) multiplier_1 (.a(in_2), .b(B), .out(out_mul));  // open: cin, cout
  BitSelector #(.width(32)) bitselector_1 (.in(in_2), .out(bitselector_1_out), .sel({5{1'b1}}));
  BitSelector #(.width(32)) bitselector_2 (.in(B), .out(bitselector_2_out), .sel({5{1'b1}}));
  BitSelector #(.width(32)) bitselector_3 (.in(out_plus), .out(bitselector_3_out), .sel({5{1'b1}}));
  BitSelector #(.width(32)) bitselector_4 (.in(out_minus), .out(bitselector_4_out), .sel({5{1'b1}}));
  xnor xnor_1 (xnor_1_out, bitselector_1_out, bitselector_2_out);
  xor xor_2 (xor_2_out, bitselector_2_out, bitselector_3_out);
  xnor xnor_2 (xnor_2_out, bitselector_2_out, bitselector_4_out);
  and and_2 (signed_cout_plus, xnor_1_out, xor_2_out);
  and and_3 (signed_cout_minus, xnor_1_out, xnor_2_out);
  Multiplexer #(.select(4), .width(32), .disabled(0), .enable("false")) multiplexer_2 (
    .in0(out_plus), .in1(out_plus), .in2(out_minus), .in3(out_minus), .in4(out_LL), .in5(out_LR),
    .in6(out_AR), .in7(out_or), .in8(out_and), .in9(out_xor), .in10(out_not), .in11(unsigned_out_comp),
    .in12(signed_out_comp), .in13(out_mul), .in14({32{1'b0}}), .in15({32{1'b0}}), .out(out), .sel(in_1));
  nor nor_1 (nor_1_out, in_1[2], in_1[3]);
  Multiplexer #(.select(2), .disabled(0)) multiplexer_3 (
    .in0(unsigned_cout_plus), .in1(signed_cout_plus), .in2(unsigned_cout_minus), .in3(signed_cout_minus),
    .out(cout), .sel(in_1[1:0]), .en(nor_1_out));

  // Other names for the same wires on the sheet: A[31:0] = in_2; S[4:0] = in_6
endmodule

module Controller (
  input  [5:0] opcode,
  input  [5:0] funct,
  output RegDst,
  output ALUSrc,
  output MemtoReg,
  output RegWrite,
  output MemWrite,
  output [2:0] Branch,
  output [1:0] Ext_Op,
  output [3:0] ALUCtrl,
  output Jump,
  output Link,
  output \return ,
  output \byte ,
  output half,
  output RegLink,
  output Sign
);

  wire Addu_2_out, addu_out, beq_out, Compu_out, ctrland_1_addu, ctrland_1_beq, ctrland_1_lui, ctrland_1_lw,
       ctrland_1_nop, ctrland_1_ori, ctrland_1_subu, ctrland_1_sw, ctrland_2_1_addu, ctrland_2_1_nop,
       ctrland_2_1_subu, lui_out, lw_out, Or_out, ori_out, Sign_Ext_out, Sll_out, Subu_2_out, subu_out,
       sw_out, Upper_Ext_out, Zero_Ext_out;

  CtrlAnd ctrland_1 (
    .opcode(opcode), .addu(ctrland_1_addu), .subu(ctrland_1_subu), .ori(ctrland_1_ori), .lw(ctrland_1_lw),
    .sw(ctrland_1_sw), .beq(ctrland_1_beq), .lui(ctrland_1_lui), .nop(ctrland_1_nop));
  CtrlAnd_2 ctrland_2_1 (.funct(funct), .addu(ctrland_2_1_addu), .subu(ctrland_2_1_subu), .nop(ctrland_2_1_nop));
  and subu (subu_out, ctrland_2_1_subu, ctrland_1_subu);
  and addu (addu_out, ctrland_2_1_addu, ctrland_1_addu);
  buf ori (ori_out, ctrland_1_ori);  // AND_Gate
  buf lw (lw_out, ctrland_1_lw);  // AND_Gate
  buf beq (beq_out, ctrland_1_beq);  // AND_Gate
  buf sw (sw_out, ctrland_1_sw);  // AND_Gate
  buf lui (lui_out, ctrland_1_lui);  // AND_Gate
  // AND_Gate nop has open pins: in0=ctrland_2_1_nop, in1=ctrland_1_nop, out=open
  or u_RegDst (RegDst, subu_out, addu_out);
  or u_ALUSrc (ALUSrc, lw_out, sw_out, lui_out, ori_out);
  buf u_MemtoReg (MemtoReg, lw_out);  // OR_Gate
  or u_RegWrite (RegWrite, lui_out, ori_out, lw_out, subu_out, addu_out);
  buf u_MemWrite (MemWrite, sw_out);  // OR_Gate
  buf More (Branch[0], 1'b0);  // OR_Gate
  buf Equal (Branch[1], beq_out);  // OR_Gate
  buf Less (Branch[2], 1'b0);  // OR_Gate
  buf Zero_Ext (Zero_Ext_out, ori_out);  // OR_Gate
  or Sign_Ext (Sign_Ext_out, lw_out, sw_out, beq_out);
  buf Upper_Ext (Upper_Ext_out, lui_out);  // OR_Gate
  or Addu_2 (Addu_2_out, lui_out, sw_out, lw_out, addu_out);
  buf Subu_2 (Subu_2_out, subu_out);  // OR_Gate
  buf Sll (Sll_out, 1'b0);  // OR_Gate
  buf Or (Or_out, ori_out);  // OR_Gate
  buf Compu (Compu_out, beq_out);  // OR_Gate
  buf u_Jump (Jump, 1'b0);  // OR_Gate
  buf u_Link (Link, 1'b0);  // OR_Gate
  buf u_return (\return , 1'b0);  // OR_Gate
  buf u_byte (\byte , 1'b0);  // OR_Gate
  buf u_half (half, 1'b0);  // OR_Gate
  buf u_RegLink (RegLink, 1'b0);  // OR_Gate
  buf u_Sign (Sign, 1'b0);  // OR_Gate
  Pull_Resistor pull_resistor_1 (.node(Ext_Op));
  Priority_Encoder #(.select(2), .disabled(0)) priority_encoder_1 (
    .in0(Zero_Ext_out), .in1(Sign_Ext_out), .in2(Upper_Ext_out), .out(Ext_Op));  // open: in3, gs, en_out, en_in
  Pull_Resistor pull_resistor_2 (.node(ALUCtrl));
  Priority_Encoder #(.select(4), .disabled(0)) priority_encoder_2 (
    .in0(Addu_2_out), .in2(Subu_2_out), .in4(Sll_out), .in7(Or_out), .in11(Compu_out), .out(ALUCtrl));  // open: in1, in3, in5, in6, in8, in9, in10, in12, in13, in14, in15, gs, en_out, en_in
endmodule

module CtrlAnd (
  input  [5:0] opcode,
  output addu,
  output subu,
  output ori,
  output lw,
  output sw,
  output beq,
  output lui,
  output nop
);

  and u_addu (addu, ~opcode[0], ~opcode[1], ~opcode[2], ~opcode[3], ~opcode[4], ~opcode[5]);  // AND_Gate
  and u_subu (subu, ~opcode[0], ~opcode[1], ~opcode[2], ~opcode[3], ~opcode[4], ~opcode[5]);  // AND_Gate
  and u_ori (ori, opcode[0], ~opcode[1], opcode[2], opcode[3], ~opcode[4], ~opcode[5]);  // AND_Gate
  and u_lw (lw, opcode[0], opcode[1], ~opcode[2], ~opcode[3], ~opcode[4], opcode[5]);  // AND_Gate
  and u_sw (sw, opcode[0], opcode[1], ~opcode[2], opcode[3], ~opcode[4], opcode[5]);  // AND_Gate
  and u_beq (beq, ~opcode[0], ~opcode[1], opcode[2], ~opcode[3], ~opcode[4], ~opcode[5]);  // AND_Gate
  and u_lui (lui, opcode[0], opcode[1], opcode[2], opcode[3], ~opcode[4], ~opcode[5]);  // AND_Gate
  and u_nop (nop, ~opcode[0], ~opcode[1], ~opcode[2], ~opcode[3], ~opcode[4], ~opcode[5]);  // AND_Gate
endmodule

module CtrlAnd_2 (
  input  [5:0] funct,
  output addu,
  output subu,
  output nop
);

  and u_addu (addu, funct[0], ~funct[1], ~funct[2], ~funct[3], ~funct[4], funct[5]);  // AND_Gate
  and u_subu (subu, funct[0], funct[1], ~funct[2], ~funct[3], ~funct[4], funct[5]);  // AND_Gate
  and u_nop (nop, ~funct[0], ~funct[1], ~funct[2], ~funct[3], ~funct[4], ~funct[5]);  // AND_Gate
endmodule

module Extender (
  input  [1:0] in_1,
  input  [15:0] in_2,
  output [31:0] out_3
);

  wire [31:0] bit_extender_1_out, bit_extender_2_out, bit_extender_3_out, shifter_1_out;

  assign bit_extender_1_out = {{16{1'b0}}, in_2};  // Bit_Extender bit_extender_1
  assign bit_extender_2_out = {{16{in_2[15]}}, in_2};  // Bit_Extender bit_extender_2
  assign bit_extender_3_out = {{16{1'b0}}, in_2};  // Bit_Extender bit_extender_3
  Shifter #(.width(32)) shifter_1 (.in(bit_extender_3_out), .\dist (5'b10000), .out(shifter_1_out));
  Multiplexer #(.select(2), .width(32), .disabled(0), .enable("false")) multiplexer_1 (
    .in0(bit_extender_1_out), .in1(bit_extender_2_out), .in2(shifter_1_out), .out(out_3), .sel(in_1));  // open: in3
  Pull_Resistor pull_resistor_1 (.node(out_3));
endmodule

module Comp (
  input  [31:0] in_1,
  output out_2,
  output out_3,
  output out_4
);

  Bit_Extender #(.in_width(32), .out_width(3), .\type ("sign")) bit_extender_1 (.in(in_1), .out({out_4, out_3, out_2}));
endmodule

module Decoder (
  input  [31:0] Instr,
  output [5:0] opcode,
  output [4:0] rs,
  output [4:0] rt,
  output [4:0] rd,
  output [4:0] shamt,
  output [5:0] funct,
  output [15:0] _16_immediate,
  output [25:0] _26_immediate
);

  Bit_Extender #(.in_width(32), .\type ("sign")) bit_extender_1 (.in(Instr), .out(_16_immediate));
  Bit_Extender #(.in_width(32), .out_width(26)) bit_extender_2 (.in(Instr), .out(_26_immediate));

  assign funct = Instr[5:0];
  assign opcode = Instr[31:26];
  assign rd = Instr[15:11];
  assign rs = Instr[25:21];
  assign rt = Instr[20:16];
  assign shamt = Instr[10:6];
endmodule

module grf (
  input  clk,
  input  reset,
  input  we,
  input  MemToReg,
  input  RegDst,
  input  Link,
  input  [31:0] AluData,
  input  RegLink,
  input  [31:0] MemData,
  input  [4:0] rs,
  input  [4:0] rt,
  input  [4:0] rd,
  input  [31:0] nPCAddr,
  output [31:0] RegData,
  output [4:0] RegAddr,
  output [31:0] RD1,
  output [31:0] RD2
);

  wire _00, _0a, _0b, _0c, _0d, _0e, _0f, _01, _1a, _1b, _1c, _1d, _1e, _1f, _02, _03, _04, _05, _06, _07,
       _08, _09, _10, _11, _12, _13, _14, _15, _16, _17, _18, _19;
  wire [4:0] multiplexer_1_out, multiplexer_2_out;
  wire [31:0] _00_prime, _0a_prime, _0b_prime, _0c_prime, _0d_prime, _0e_prime, _0f_prime, _01_prime,
       _1a_prime, _1b_prime, _1c_prime, _1d_prime, _1e_prime, _1f_prime, _02_prime, _03_prime, _04_prime,
       _05_prime, _06_prime, _07_prime, _08_prime, _09_prime, _10_prime, _11_prime, _12_prime, _13_prime,
       _14_prime, _15_prime, _16_prime, _17_prime, _18_prime, _19_prime, multiplexer_4_out;

  Multiplexer #(.width(5), .enable("false")) multiplexer_1 (
    .in0({5{1'b1}}), .in1(rd), .out(multiplexer_1_out), .sel(RegLink));
  Demultiplexer #(.select(5), .enable("false")) demultiplexer_1 (
    .out0(_00), .out1(_01), .out2(_02), .out3(_03), .out4(_04), .out5(_05), .out6(_06), .out7(_07),
    .out8(_08), .out9(_09), .out10(_0a), .out11(_0b), .out12(_0c), .out13(_0d), .out14(_0e), .out15(_0f),
    .out16(_10), .out17(_11), .out18(_12), .out19(_13), .out20(_14), .out21(_15), .out22(_16), .out23(_17),
    .out24(_18), .out25(_19), .out26(_1a), .out27(_1b), .out28(_1c), .out29(_1d), .out30(_1e), .out31(_1f),
    .in(we), .sel(RegAddr));
  Multiplexer #(.width(5), .enable("false")) multiplexer_2 (.in0(rt), .in1(rd), .out(multiplexer_2_out), .sel(RegDst));
  Multiplexer #(.width(5), .enable("false")) multiplexer_3 (
    .in0(multiplexer_2_out), .in1(multiplexer_1_out), .out(RegAddr), .sel(Link));
  Multiplexer #(.width(32), .enable("false")) multiplexer_4 (
    .in0(AluData), .in1(MemData), .out(multiplexer_4_out), .sel(MemToReg));
  Multiplexer #(.width(32), .enable("false")) multiplexer_5 (
    .in0(multiplexer_4_out), .in1(nPCAddr), .out(RegData), .sel(Link));
  Multiplexer #(.select(5), .width(32), .enable("false")) multiplexer_6 (
    .in0(_00_prime), .in1(_01_prime), .in2(_02_prime), .in3(_03_prime), .in4(_04_prime), .in5(_05_prime),
    .in6(_06_prime), .in7(_07_prime), .in8(_08_prime), .in9(_09_prime), .in10(_0a_prime), .in11(_0b_prime),
    .in12(_0c_prime), .in13(_0d_prime), .in14(_0e_prime), .in15(_0f_prime), .in16(_10_prime),
    .in17(_11_prime), .in18(_12_prime), .in19(_13_prime), .in20(_14_prime), .in21(_15_prime),
    .in22(_16_prime), .in23(_17_prime), .in24(_18_prime), .in25(_19_prime), .in26(_1a_prime),
    .in27(_1b_prime), .in28(_1c_prime), .in29(_1d_prime), .in30(_1e_prime), .in31(_1f_prime), .out(RD1),
    .sel(rs));
  Register #(.width(32)) u__00 (.D(RegData), .en(1'b0), .Q(_00_prime), .clk(clk), .clr(reset));
  Register #(.width(32)) u__01 (.D(RegData), .en(_01), .Q(_01_prime), .clk(clk), .clr(reset));
  Register #(.width(32)) u__02 (.D(RegData), .en(_02), .Q(_02_prime), .clk(clk), .clr(reset));
  Register #(.width(32)) u__03 (.D(RegData), .en(_03), .Q(_03_prime), .clk(clk), .clr(reset));
  Register #(.width(32)) u__04 (.D(RegData), .en(_04), .Q(_04_prime), .clk(clk), .clr(reset));
  Register #(.width(32)) u__05 (.D(RegData), .en(_05), .Q(_05_prime), .clk(clk), .clr(reset));
  Register #(.width(32)) u__06 (.D(RegData), .en(_06), .Q(_06_prime), .clk(clk), .clr(reset));
  Register #(.width(32)) u__07 (.D(RegData), .en(_07), .Q(_07_prime), .clk(clk), .clr(reset));
  Multiplexer #(.select(5), .width(32), .enable("false")) multiplexer_7 (
    .in0(_00_prime), .in1(_01_prime), .in2(_02_prime), .in3(_03_prime), .in4(_04_prime), .in5(_05_prime),
    .in6(_06_prime), .in7(_07_prime), .in8(_08_prime), .in9(_09_prime), .in10(_0a_prime), .in11(_0b_prime),
    .in12(_0c_prime), .in13(_0d_prime), .in14(_0e_prime), .in15(_0f_prime), .in16(_10_prime),
    .in17(_11_prime), .in18(_12_prime), .in19(_13_prime), .in20(_14_prime), .in21(_15_prime),
    .in22(_16_prime), .in23(_17_prime), .in24(_18_prime), .in25(_19_prime), .in26(_1a_prime),
    .in27(_1b_prime), .in28(_1c_prime), .in29(_1d_prime), .in30(_1e_prime), .in31(_1f_prime), .out(RD2),
    .sel(rt));
  Register #(.width(32)) u__08 (.D(RegData), .en(_08), .Q(_08_prime), .clk(clk), .clr(reset));
  Register #(.width(32)) u__09 (.D(RegData), .en(_09), .Q(_09_prime), .clk(clk), .clr(reset));
  Register #(.width(32)) u__0a (.D(RegData), .en(_0a), .Q(_0a_prime), .clk(clk), .clr(reset));
  Register #(.width(32)) u__0b (.D(RegData), .en(_0b), .Q(_0b_prime), .clk(clk), .clr(reset));
  Register #(.width(32)) u__0c (.D(RegData), .en(_0c), .Q(_0c_prime), .clk(clk), .clr(reset));
  Register #(.width(32)) u__0d (.D(RegData), .en(_0d), .Q(_0d_prime), .clk(clk), .clr(reset));
  Register #(.width(32)) u__0e (.D(RegData), .en(_0e), .Q(_0e_prime), .clk(clk), .clr(reset));
  Register #(.width(32)) u__0f (.D(RegData), .en(_0f), .Q(_0f_prime), .clk(clk), .clr(reset));
  Register #(.width(32)) u__10 (.D(RegData), .en(_10), .Q(_10_prime), .clk(clk), .clr(reset));
  Register #(.width(32)) u__11 (.D(RegData), .en(_11), .Q(_11_prime), .clk(clk), .clr(reset));
  Register #(.width(32)) u__12 (.D(RegData), .en(_12), .Q(_12_prime), .clk(clk), .clr(reset));
  Register #(.width(32)) u__13 (.D(RegData), .en(_13), .Q(_13_prime), .clk(clk), .clr(reset));
  Register #(.width(32)) u__14 (.D(RegData), .en(_14), .Q(_14_prime), .clk(clk), .clr(reset));
  Register #(.width(32)) u__15 (.D(RegData), .en(_15), .Q(_15_prime), .clk(clk), .clr(reset));
  Register #(.width(32)) u__16 (.D(RegData), .en(_16), .Q(_16_prime), .clk(clk), .clr(reset));
  Register #(.width(32)) u__17 (.D(RegData), .en(_17), .Q(_17_prime), .clk(clk), .clr(reset));
  Register #(.width(32)) u__18 (.D(RegData), .en(_18), .Q(_18_prime), .clk(clk), .clr(reset));
  Register #(.width(32)) u__19 (.D(RegData), .en(_19), .Q(_19_prime), .clk(clk), .clr(reset));
  Register #(.width(32)) u__1a (.D(RegData), .en(_1a), .Q(_1a_prime), .clk(clk), .clr(reset));
  Register #(.width(32)) u__1b (.D(RegData), .en(_1b), .Q(_1b_prime), .clk(clk), .clr(reset));
  Register #(.width(32)) u__1c (.D(RegData), .en(_1c), .Q(_1c_prime), .clk(clk), .clr(reset));
  Register #(.width(32)) u__1d (.D(RegData), .en(_1d), .Q(_1d_prime), .clk(clk), .clr(reset));
  Register #(.width(32)) u__1e (.D(RegData), .en(_1e), .Q(_1e_prime), .clk(clk), .clr(reset));
  Register #(.width(32)) u__1f (.D(RegData), .en(_1f), .Q(_1f_prime), .clk(clk), .clr(reset));

  // Other names for the same wires on the sheet: A1[4:0] = rs; A2[4:0] = rt; A3[4:0] = RegAddr; data[31:0] = RegData
endmodule

module MemData (
  input  Byte,
  input  Half,
  input  Sign,
  input  [31:0] in_4,
  output [31:0] out_5
);

  wire [7:0] bit_extender_1_out, bit_extender_5_out;
  wire [15:0] bit_extender_4_out, bit_extender_7_out;
  wire [31:0] bit_extender_2_out, bit_extender_3_out, bit_extender_6_out, bit_extender_8_out,
       multiplexer_1_out, multiplexer_2_out, multiplexer_3_out, multiplexer_4_out;

  Bit_Extender #(.in_width(32), .out_width(8)) bit_extender_1 (.in(in_4), .out(bit_extender_1_out));
  assign bit_extender_2_out = {{24{1'b0}}, bit_extender_1_out};  // Bit_Extender bit_extender_2
  assign bit_extender_3_out = {{16{1'b0}}, bit_extender_4_out};  // Bit_Extender bit_extender_3
  Bit_Extender #(.in_width(32)) bit_extender_4 (.in(in_4), .out(bit_extender_4_out));
  Bit_Extender #(.in_width(32), .out_width(8), .\type ("sign")) bit_extender_5 (.in(in_4), .out(bit_extender_5_out));
  assign bit_extender_6_out = {{24{bit_extender_5_out[7]}}, bit_extender_5_out};  // Bit_Extender bit_extender_6
  Bit_Extender #(.in_width(32), .\type ("sign")) bit_extender_7 (.in(in_4), .out(bit_extender_7_out));
  assign bit_extender_8_out = {{16{bit_extender_7_out[15]}}, bit_extender_7_out};  // Bit_Extender bit_extender_8
  Multiplexer #(.width(32), .enable("false")) multiplexer_1 (
    .in0(in_4), .in1(bit_extender_2_out), .out(multiplexer_1_out), .sel(Byte));
  Multiplexer #(.width(32), .enable("false")) multiplexer_2 (
    .in1(bit_extender_6_out), .out(multiplexer_2_out), .sel(Byte));  // open: in0
  Multiplexer #(.width(32), .enable("false")) multiplexer_3 (
    .in0(multiplexer_1_out), .in1(bit_extender_3_out), .out(multiplexer_3_out), .sel(Half));
  Multiplexer #(.width(32), .enable("false")) multiplexer_4 (
    .in0(multiplexer_2_out), .in1(bit_extender_8_out), .out(multiplexer_4_out), .sel(Half));
  Multiplexer #(.width(32), .enable("false")) multiplexer_5 (
    .in0(multiplexer_3_out), .in1(multiplexer_4_out), .out(out_5), .sel(Sign));
endmodule
