// Logisim project p3-3.circ as structural Verilog: 13 circuits, main circuit main
module main (
  input  in_1,
  output [31:0] instr,
  output RegWrite,
  output [4:0] RegAddr,
  output [31:0] RegData,
  output MemWrite,
  output [4:0] MemAddr,
  output [31:0] MemData
);

  wire and_1_out, and_2_out, and_3_out, and_4_out, Branch, Byte, Clk, comp_1_beq, comp_1_bgt, comp_1_blt,
       controller_1_alusrc, controller_1_bytecat, controller_1_link, controller_1_memtoreg,
       controller_1_sign, Half, Jump, Return;
  wire [1:0] controller_1_regdst, ExtCtrl, Offset;
  wire [2:0] B;
  wire [3:0] AluCtrl;
  wire [4:0] rd, rs, rt, shamt;
  wire [5:0] funct, opcode;
  wire [15:0] instr_decoder_1_imm16;
  wire [23:0] bit_extender_1_out, bit_extender_3_out;
  wire [25:0] instr_decoder_1_imm26;
  wire [31:0] adder_2_out, adder_3_out, Addr, alu_1_out_7, BranchAddr, grf_1_rd2, imm, JumpAddr,
       npc_sel_1_out_6, ram_1_data, register_1_q, shifter_1_out, shifter_2_out, shifter_3_out,
       subtractor_1_out, subtractor_2_out;

  Clock clock_1 (.out(Clk));
  Controller controller_1 (
    .opcode(opcode), .funct(funct), .RegDst(controller_1_regdst), .AluSrc(controller_1_alusrc),
    .RegWrite(RegWrite), .MemToReg(controller_1_memtoreg), .MemWrite(MemWrite), .Jump(Jump),
    .Link(controller_1_link), .AluCtrl(AluCtrl), .ExtCtrl(ExtCtrl), .Branch(B), .Byte(Byte), .Half(Half),
    .Sign(controller_1_sign), .Return(Return), .wsbh(shamt), .ByteCat(controller_1_bytecat));
  nPC_Sel npc_sel_1 (
    .nPC_4(adder_3_out), .BranchAddr(BranchAddr), .JumpAddr(JumpAddr), .Branch(Branch), .Jump(Jump),
    .out_6(npc_sel_1_out_6));
  Shifter #(.width(32)) shifter_1 (.in(adder_3_out), .\dist (5'b00010), .out(shifter_1_out));
  Adder #(.width(32)) adder_1 (.a(imm), .b(adder_3_out), .out(BranchAddr));  // open: cin, cout
  Register #(.width(32)) register_1 (.D(npc_sel_1_out_6), .Q(register_1_q), .clk(Clk), .clr(in_1));  // open: en
  Adder #(.width(32)) adder_2 (.a(shifter_1_out), .b(32'h3000), .out(adder_2_out));  // open: cin, cout
  Adder #(.width(32)) adder_3 (.a(register_1_q), .b(32'h1), .out(adder_3_out));  // open: cin, cout
  Bit_Extender #(.in_width(32), .out_width(24)) bit_extender_1 (.in(register_1_q), .out(bit_extender_1_out));
  ROM #(.addrWidth(24), .dataWidth(32)) rom_1 (.addr(bit_extender_1_out), .data(instr));  // open: sel
  Instr_Decoder instr_decoder_1 (
    .in_1(instr), .opcode(opcode), .rs(rs), .rt(rt), .rd(rd), .shamt(shamt), .funct(funct),
    .imm16(instr_decoder_1_imm16), .imm26(instr_decoder_1_imm26));
  Extender extender_1 (.in_2(instr_decoder_1_imm16), .in_3(instr_decoder_1_imm26), .out_4(imm), .in_1(ExtCtrl));
  Subtractor #(.width(32)) subtractor_1 (.a(imm), .b(32'hc00), .out(subtractor_1_out));  // open: bin, bout
  Subtractor #(.width(32)) subtractor_2 (.a(Addr), .b(32'h3000), .out(subtractor_2_out));  // open: bin, bout
  GRF grf_1 (
    .rs(rs), .rt(rt), .rd(rd), .AluData(alu_1_out_7), .MemData(ram_1_data), .nPCAddr(adder_2_out),
    .RegAddr(RegAddr), .RegData(RegData), .RD1(Addr), .RD2(grf_1_rd2), .RegDst(controller_1_regdst),
    .MemToReg(controller_1_memtoreg), .clk(Clk), .reset(in_1), .we(RegWrite), .Byte(Byte), .Half(Half),
    .Sign(controller_1_sign), .Offset(Offset), .Link(controller_1_link), .ByteCat(controller_1_bytecat));
  Shifter #(.width(32), .shift("lr")) shifter_2 (.in(subtractor_2_out), .\dist (5'b00010), .out(shifter_2_out));
  Multiplexer #(.width(32), .enable("false")) multiplexer_1 (
    .in0(subtractor_1_out), .in1(shifter_2_out), .out(JumpAddr), .sel(Return));
  ALU alu_1 (
    .A(Addr), .B(grf_1_rd2), .imm(imm), .Shamt(shamt), .out_7(alu_1_out_7), .AluSrc(controller_1_alusrc),
    .AluCtrl(AluCtrl));
  // Probe on grf_1_rd2
  Comp comp_1 (.in_1(alu_1_out_7), .bgt(comp_1_bgt), .beq(comp_1_beq), .blt(comp_1_blt));
  BitSelector #(.width(32), .group(2)) bitselector_1 (.in(alu_1_out_7), .out(Offset), .sel(4'b0000));
  Shifter #(.width(32), .shift("lr")) shifter_3 (.in(alu_1_out_7), .\dist (5'b00010), .out(shifter_3_out));
  and and_1 (and_1_out, B[0], B[1], B[2]);
  and and_2 (and_2_out, comp_1_bgt, B[0]);
  and and_3 (and_3_out, comp_1_beq, B[1]);
  and and_4 (and_4_out, comp_1_blt, B[2]);
  // Probe on MemData
  StoreType storetype_1 (
    .RegData(grf_1_rd2), .offset(Offset), .MemData(ram_1_data), .out_6(MemData), .Byte(Byte), .Half(Half));
  // Probe on instr
  // Probe on RegData
  // Probe on MemData
  or or_1 (Branch, and_1_out, and_2_out, and_3_out, and_4_out);
  Bit_Extender #(.in_width(32), .out_width(5)) bit_extender_2 (.in(shifter_3_out), .out(MemAddr));
  Bit_Extender #(.in_width(32), .out_width(24)) bit_extender_3 (.in(shifter_3_out), .out(bit_extender_3_out));
  RAM #(.addrWidth(24), .dataWidth(32), .bus("separate")) ram_1 (
    .addr(bit_extender_3_out), .din(MemData), .data(ram_1_data), .str(MemWrite), .clk(Clk), .clr(in_1));  // open: sel, ld

  // Other names for the same wires on the sheet: Reset = in_1

  // Notes on the sheet:
  //   contents of rom_1 (hex, n*v repeats v):
  //   34081234 11000004 3409ffff 11000010 1094021 1100fffc 3c010000 34210000 1014021 11000004 3c01ffff
  //   3421ffff 1014021 1100fff6 350804d2 11000008 3c010000 3421ffff 14821 11000002 3c08ffff 1100ffea
  //   1284023 1100fff2 1284823 1100fff6
endmodule

module ALU (
  input  [3:0] AluCtrl,
  input  [31:0] A,
  input  AluSrc,
  input  [31:0] B,
  input  [31:0] imm,
  input  [4:0] Shamt,
  output [31:0] out_7
);

  wire [2:0] comparator_1_gt, comparator_2_gt;
  wire [31:0] AddOut, AndOut, B_t, CompOut, CompuOut, OrOut, SllOut, SraOut, SrlOut, SubOut, XorOut;

  Multiplexer #(.width(32), .enable("false")) multiplexer_1 (.in0(B), .in1(imm), .out(B_t), .sel(AluSrc));
  Adder #(.width(32)) adder_1 (.a(A), .b(B_t), .out(AddOut));  // open: cin, cout
  Subtractor #(.width(32)) subtractor_1 (.a(A), .b(B_t), .out(SubOut));  // open: bin, bout
  Shifter #(.width(32)) shifter_1 (.in(B_t), .\dist (Shamt), .out(SllOut));
  Shifter #(.width(32), .shift("lr")) shifter_2 (.in(B_t), .\dist (Shamt), .out(SrlOut));
  Shifter #(.width(32), .shift("ar")) shifter_3 (.in(B_t), .\dist (Shamt), .out(SraOut));
  assign AndOut = A & B_t;  // AND_Gate and_1, 32 bits wide
  assign OrOut = A | B_t;  // OR_Gate or_1, 32 bits wide
  assign XorOut = A ^ B_t;  // XOR_Gate xor_1, 32 bits wide
  Comparator #(.width(32), .mode("unsigned")) comparator_1 (
    .a(A), .b(B_t), .gt(comparator_1_gt[0]), .eq(comparator_1_gt[1]), .lt(comparator_1_gt[2]));
  Comparator #(.width(32)) comparator_2 (
    .a(A), .b(B_t), .gt(comparator_2_gt[0]), .eq(comparator_2_gt[1]), .lt(comparator_2_gt[2]));
  assign CompuOut = {{29{1'b0}}, comparator_1_gt};  // Bit_Extender bit_extender_1
  assign CompOut = {{29{1'b0}}, comparator_2_gt};  // Bit_Extender bit_extender_2
  Multiplexer #(.select(4), .width(32), .enable("false")) multiplexer_2 (
    .in0(AddOut), .in1(SubOut), .in2(SllOut), .in3(SrlOut), .in4(SraOut), .in5(AndOut), .in6(OrOut),
    .in7(XorOut), .in8(CompuOut), .in9(CompOut), .in10({B_t[23:16], B_t[31:24], B_t[7:0], B_t[15:8]}),
    .out(out_7), .sel(AluCtrl));  // open: in11, in12, in13, in14, in15

  // Other names for the same wires on the sheet: SwapOut[31:0] = {B_t[23:16], B_t[31:24], B_t[7:0], B_t[15:8]};
  //   S[4:0] = Shamt
endmodule

module GRF (
  input  clk,
  input  reset,
  input  we,
  input  [1:0] RegDst,
  input  [4:0] rs,
  input  [4:0] rt,
  input  [4:0] rd,
  input  Byte,
  input  Half,
  input  Sign,
  input  ByteCat,
  input  [31:0] AluData,
  input  MemToReg,
  input  Link,
  input  [31:0] MemData,
  input  [1:0] Offset,
  input  [31:0] nPCAddr,
  output [4:0] RegAddr,
  output [31:0] RegData,
  output [31:0] RD1,
  output [31:0] RD2
);

  wire _00, _0a, _0b, _0c, _0d, _0e, _0f, _01, _1a, _1b, _1c, _1d, _1e, _1f, _02, _03, _04, _05, _06, _07,
       _08, _09, _10, _11, _12, _13, _14, _15, _16, _17, _18, _19;
  wire [31:0] _00_prime, _0a_prime, _0b_prime, _0c_prime, _0d_prime, _0e_prime, _0f_prime, _01_prime,
       _1a_prime, _1b_prime, _1c_prime, _1d_prime, _1e_prime, _1f_prime, _02_prime, _03_prime, _04_prime,
       _05_prime, _06_prime, _07_prime, _08_prime, _09_prime, _10_prime, _11_prime, _12_prime, _13_prime,
       _14_prime, _15_prime, _16_prime, _17_prime, _18_prime, _19_prime, datatype_1_out_6, loadtype_1_out_6,
       multiplexer_2_out, multiplexer_3_out;

  Demultiplexer #(.select(5), .enable("false")) demultiplexer_1 (
    .out0(_00), .out1(_01), .out2(_02), .out3(_03), .out4(_04), .out5(_05), .out6(_06), .out7(_07),
    .out8(_08), .out9(_09), .out10(_0a), .out11(_0b), .out12(_0c), .out13(_0d), .out14(_0e), .out15(_0f),
    .out16(_10), .out17(_11), .out18(_12), .out19(_13), .out20(_14), .out21(_15), .out22(_16), .out23(_17),
    .out24(_18), .out25(_19), .out26(_1a), .out27(_1b), .out28(_1c), .out29(_1d), .out30(_1e), .out31(_1f),
    .in(we), .sel(RegAddr));
  Multiplexer #(.select(2), .width(5), .enable("false")) multiplexer_1 (
    .in0(rt), .in1(rd), .in2({5{1'b1}}), .out(RegAddr), .sel(RegDst));  // open: in3
  Multiplexer #(.width(32), .enable("false")) multiplexer_2 (
    .in0(AluData), .in1(MemData), .out(multiplexer_2_out), .sel(MemToReg));
  Multiplexer #(.width(32), .enable("false")) multiplexer_3 (
    .in0(multiplexer_2_out), .in1(nPCAddr), .out(multiplexer_3_out), .sel(Link));
  DataType datatype_1 (
    .Data(multiplexer_3_out), .out_6(datatype_1_out_6), .Byte(Byte), .Half(Half), .Sign(Sign), .Offset(Offset));
  LoadType loadtype_1 (
    .RegData(multiplexer_3_out), .offset(Offset), .MemData(RD2), .out_6(loadtype_1_out_6), .Byte(Byte),
    .Half(Half));
  Multiplexer #(.width(32), .enable("false")) multiplexer_4 (
    .in0(datatype_1_out_6), .in1(loadtype_1_out_6), .out(RegData), .sel(ByteCat));
  Multiplexer #(.select(5), .width(32), .enable("false")) multiplexer_5 (
    .in0(_00_prime), .in1(_01_prime), .in2(_02_prime), .in3(_03_prime), .in4(_04_prime), .in5(_05_prime),
    .in6(_06_prime), .in7(_07_prime), .in8(_08_prime), .in9(_09_prime), .in10(_0a_prime), .in11(_0b_prime),
    .in12(_0c_prime), .in13(_0d_prime), .in14(_0e_prime), .in15(_0f_prime), .in16(_10_prime),
    .in17(_11_prime), .in18(_12_prime), .in19(_13_prime), .in20(_14_prime), .in21(_15_prime),
    .in22(_16_prime), .in23(_17_prime), .in24(_18_prime), .in25(_19_prime), .in26(_1a_prime),
    .in27(_1b_prime), .in28(_1c_prime), .in29(_1d_prime), .in30(_1e_prime), .in31(_1f_prime), .out(RD1),
    .sel(rs));
  Register #(.width(32)) u__00 (.D(RegData), .en(1'b0), .Q(_00_prime), .clk(clk), .clr(reset));
  Register #(.width(32)) u__01 (.D(RegData), .en(_01), .Q(_01_prime), .clk(clk), .clr(reset));
  Register #(.width(32)) u__02 (.D(RegData), .en(_02), .Q(_02_prime), .clk(clk), .clr(reset));
  Register #(.width(32)) u__03 (.D(RegData), .en(_03), .Q(_03_prime), .clk(clk), .clr(reset));
  Register #(.width(32)) u__04 (.D(RegData), .en(_04), .Q(_04_prime), .clk(clk), .clr(reset));
  Register #(.width(32)) u__05 (.D(RegData), .en(_05), .Q(_05_prime), .clk(clk), .clr(reset));
  Register #(.width(32)) u__06 (.D(RegData), .en(_06), .Q(_06_prime), .clk(clk), .clr(reset));
  Register #(.width(32)) u__07 (.D(RegData), .en(_07), .Q(_07_prime), .clk(clk), .clr(reset));
  Multiplexer #(.select(5), .width(32), .enable("false")) multiplexer_6 (
    .in0(_00_prime), .in1(_01_prime), .in2(_02_prime), .in3(_03_prime), .in4(_04_prime), .in5(_05_prime),
    .in6(_06_prime), .in7(_07_prime), .in8(_08_prime), .in9(_09_prime), .in10(_0a_prime), .in11(_0b_prime),
    .in12(_0c_prime), .in13(_0d_prime), .in14(_0e_prime), .in15(_0f_prime), .in16(_10_prime),
    .in17(_11_prime), .in18(_12_prime), .in19(_13_prime), .in20(_14_prime), .in21(_15_prime),
    .in22(_16_prime), .in23(_17_prime), .in24(_18_prime), .in25(_19_prime), .in26(_1a_prime),
    .in27(_1b_prime), .in28(_1c_prime), .in29(_1d_prime), .in30(_1e_prime), .in31(_1f_prime), .out(RD2),
    .sel(rt));
  Register #(.width(32)) u__08 (.D(RegData), .en(_08), .Q(_08_prime), .clk(clk), .clr(reset));
  Register #(.width(32)) u__09 (.D(RegData), .en(_09), .Q(_09_prime), .clk(clk), .clr(reset));
  Register #(.width(32)) u__0a (.D(RegData), .en(_0a), .Q(_0a_prime), .clk(clk), .clr(reset));
  Register #(.width(32)) u__0b (.D(RegData), .en(_0b), .Q(_0b_prime), .clk(clk), .clr(reset));
  Register #(.width(32)) u__0c (.D(RegData), .en(_0c), .Q(_0c_prime), .clk(clk), .clr(reset));
  Register #(.width(32)) u__0d (.D(RegData), .en(_0d), .Q(_0d_prime), .clk(clk), .clr(reset));
  Register #(.width(32)) u__0e (.D(RegData), .en(_0e), .Q(_0e_prime), .clk(clk), .clr(reset));
  Register #(.width(32)) u__0f (.D(RegData), .en(_0f), .Q(_0f_prime), .clk(clk), .clr(reset));
  Register #(.width(32)) u__10 (.D(RegData), .en(_10), .Q(_10_prime), .clk(clk), .clr(reset));
  Register #(.width(32)) u__11 (.D(RegData), .en(_11), .Q(_11_prime), .clk(clk), .clr(reset));
  Register #(.width(32)) u__12 (.D(RegData), .en(_12), .Q(_12_prime), .clk(clk), .clr(reset));
  Register #(.width(32)) u__13 (.D(RegData), .en(_13), .Q(_13_prime), .clk(clk), .clr(reset));
  Register #(.width(32)) u__14 (.D(RegData), .en(_14), .Q(_14_prime), .clk(clk), .clr(reset));
  Register #(.width(32)) u__15 (.D(RegData), .en(_15), .Q(_15_prime), .clk(clk), .clr(reset));
  Register #(.width(32)) u__16 (.D(RegData), .en(_16), .Q(_16_prime), .clk(clk), .clr(reset));
  Register #(.width(32)) u__17 (.D(RegData), .en(_17), .Q(_17_prime), .clk(clk), .clr(reset));
  Register #(.width(32)) u__18 (.D(RegData), .en(_18), .Q(_18_prime), .clk(clk), .clr(reset));
  Register #(.width(32)) u__19 (.D(RegData), .en(_19), .Q(_19_prime), .clk(clk), .clr(reset));
  Register #(.width(32)) u__1a (.D(RegData), .en(_1a), .Q(_1a_prime), .clk(clk), .clr(reset));
  Register #(.width(32)) u__1b (.D(RegData), .en(_1b), .Q(_1b_prime), .clk(clk), .clr(reset));
  Register #(.width(32)) u__1c (.D(RegData), .en(_1c), .Q(_1c_prime), .clk(clk), .clr(reset));
  Register #(.width(32)) u__1d (.D(RegData), .en(_1d), .Q(_1d_prime), .clk(clk), .clr(reset));
  Register #(.width(32)) u__1e (.D(RegData), .en(_1e), .Q(_1e_prime), .clk(clk), .clr(reset));
  Register #(.width(32)) u__1f (.D(RegData), .en(_1f), .Q(_1f_prime), .clk(clk), .clr(reset));

  // Other names for the same wires on the sheet: A1[4:0] = rs; A2[4:0] = rt; A3[4:0] = RegAddr; data[31:0] = RegData
endmodule

module Instr_Decoder (
  input  [31:0] in_1,
  output [5:0] opcode,
  output [4:0] rs,
  output [4:0] rt,
  output [4:0] rd,
  output [4:0] shamt,
  output [5:0] funct,
  output [15:0] imm16,
  output [25:0] imm26
);

  Bit_Extender #(.in_width(32)) bit_extender_1 (.in(in_1), .out(imm16));
  Bit_Extender #(.in_width(32), .out_width(26)) bit_extender_2 (.in(in_1), .out(imm26));

  assign funct = in_1[5:0];
  assign opcode = in_1[31:26];
  assign rd = in_1[15:11];
  assign rs = in_1[25:21];
  assign rt = in_1[20:16];
  assign shamt = in_1[10:6];
endmodule

module nPC_Sel (
  input  Branch,
  input  Jump,
  input  [31:0] nPC_4,
  input  [31:0] BranchAddr,
  input  [31:0] JumpAddr,
  output [31:0] out_6
);

  wire [31:0] multiplexer_1_out;

  Multiplexer #(.width(32), .enable("false")) multiplexer_1 (
    .in0(nPC_4), .in1(BranchAddr), .out(multiplexer_1_out), .sel(Branch));
  Multiplexer #(.width(32), .enable("false")) multiplexer_2 (
    .in0(multiplexer_1_out), .in1(JumpAddr), .out(out_6), .sel(Jump));
endmodule

module DataType (
  input  Byte,
  input  Half,
  input  Sign,
  input  [31:0] Data,
  input  [1:0] Offset,
  output [31:0] out_6
);

  wire Half_t;
  wire [7:0] bitselector_1_out, bitselector_3_out;
  wire [15:0] bitselector_2_out, bitselector_4_out;
  wire [31:0] bit_extender_1_out, bit_extender_2_out, bit_extender_3_out, bit_extender_4_out,
       multiplexer_1_out, multiplexer_2_out, multiplexer_3_out, multiplexer_4_out;

  BitSelector #(.width(32), .group(8)) bitselector_1 (.in(Data), .out(bitselector_1_out), .sel(Offset));
  BitSelector #(.width(32), .group(16)) bitselector_2 (.in(Data), .out(bitselector_2_out), .sel(Half_t));
  BitSelector #(.width(32), .group(8)) bitselector_3 (.in(Data), .out(bitselector_3_out), .sel(Offset));
  BitSelector #(.width(32), .group(16)) bitselector_4 (.in(Data), .out(bitselector_4_out), .sel(Half_t));
  BitSelector #(.width(2)) bitselector_5 (.in(Offset), .out(Half_t), .sel(1'b1));
  Multiplexer #(.width(32), .enable("false")) multiplexer_1 (
    .in0(Data), .in1(bit_extender_1_out), .out(multiplexer_1_out), .sel(Byte));
  assign bit_extender_1_out = {{24{1'b0}}, bitselector_1_out};  // Bit_Extender bit_extender_1
  assign bit_extender_2_out = {{16{1'b0}}, bitselector_2_out};  // Bit_Extender bit_extender_2
  Multiplexer #(.width(32), .enable("false")) multiplexer_2 (
    .in0(Data), .in1(bit_extender_3_out), .out(multiplexer_2_out), .sel(Byte));
  assign bit_extender_3_out = {{24{bitselector_3_out[7]}}, bitselector_3_out};  // Bit_Extender bit_extender_3
  assign bit_extender_4_out = {{16{bitselector_4_out[15]}}, bitselector_4_out};  // Bit_Extender bit_extender_4
  Multiplexer #(.width(32), .enable("false")) multiplexer_3 (
    .in0(multiplexer_1_out), .in1(bit_extender_2_out), .out(multiplexer_3_out), .sel(Half));
  Multiplexer #(.width(32), .enable("false")) multiplexer_4 (
    .in0(multiplexer_2_out), .in1(bit_extender_4_out), .out(multiplexer_4_out), .sel(Half));
  Multiplexer #(.width(32), .enable("false")) multiplexer_5 (
    .in0(multiplexer_3_out), .in1(multiplexer_4_out), .out(out_6), .sel(Sign));

  // Other names for the same wires on the sheet: Byte_t[1:0] = Offset
endmodule

module Extender (
  input  [1:0] in_1,
  input  [15:0] in_2,
  input  [25:0] in_3,
  output [31:0] out_4
);

  wire [31:0] bit_extender_1_out, bit_extender_2_out, bit_extender_3_out, bit_extender_4_out, shifter_1_out;

  assign bit_extender_1_out = {{16{1'b0}}, in_2};  // Bit_Extender bit_extender_1
  assign bit_extender_2_out = {{16{1'b0}}, in_2};  // Bit_Extender bit_extender_2
  assign bit_extender_3_out = {{16{in_2[15]}}, in_2};  // Bit_Extender bit_extender_3
  Shifter #(.width(32)) shifter_1 (.in(bit_extender_1_out), .\dist (5'b10000), .out(shifter_1_out));
  assign bit_extender_4_out = {{6{1'b0}}, in_3};  // Bit_Extender bit_extender_4
  Multiplexer #(.select(2), .width(32), .enable("false")) multiplexer_1 (
    .in0(bit_extender_2_out), .in1(bit_extender_3_out), .in2(shifter_1_out), .in3(bit_extender_4_out),
    .out(out_4), .sel(in_1));
endmodule

module Comp (
  input  [31:0] in_1,
  output bgt,
  output beq,
  output blt
);

  Bit_Extender #(.in_width(32), .out_width(3), .\type ("sign")) bit_extender_1 (.in(in_1), .out({blt, beq, bgt}));
endmodule

module Controller (
  input  [5:0] opcode,
  input  [4:0] wsbh,
  input  [5:0] funct,
  output [1:0] RegDst,
  output AluSrc,
  output RegWrite,
  output MemToReg,
  output MemWrite,
  output [2:0] Branch,
  output Jump,
  output Link,
  output Return,
  output Byte,
  output Half,
  output Sign,
  output ByteCat,
  output [3:0] AluCtrl,
  output [1:0] ExtCtrl
);

  wire add_out, addu_out, and_out, balr_out, beq_out, comp_out, comparator_1_eq, compu_out, Ext_26_out,
       Ext_Sign_out, Ext_Up_out, Ext_Zero_out, funct_1_addu, funct_1_jalr, funct_1_jr, funct_1_sll,
       funct_1_subu, funct_1_wsbh, jal_out, jalr_out, jr_out, lb_out, lbi_out, lh_out, lui_out, lw_out,
       opcode_1_addu, opcode_1_balr, opcode_1_beq, opcode_1_jal, opcode_1_jalr, opcode_1_jr, opcode_1_lb,
       opcode_1_lbi, opcode_1_lh, opcode_1_lui, opcode_1_lw, opcode_1_ori, opcode_1_sb, opcode_1_sh,
       opcode_1_sll, opcode_1_subu, opcode_1_sw, opcode_1_wsbh, or_out, ori_out, RegDst_2_out, RegDst_3_out,
       RegDst_out, sb_out, sh_out, sll_2_out, sll_out, sra_out, srl_out, sub_out, subu_out, sw_out, swap_out,
       wsbh_out, xor_out;

  opcode opcode_1 (
    .opcode(opcode), .addu(opcode_1_addu), .subu(opcode_1_subu), .ori(opcode_1_ori), .lw(opcode_1_lw),
    .sw(opcode_1_sw), .beq(opcode_1_beq), .lui(opcode_1_lui), .jal(opcode_1_jal), .jr(opcode_1_jr),
    .jalr(opcode_1_jalr), .lb(opcode_1_lb), .lh(opcode_1_lh), .sb(opcode_1_sb), .sh(opcode_1_sh),
    .sll(opcode_1_sll), .balr(opcode_1_balr), .wsbh(opcode_1_wsbh), .lbi(opcode_1_lbi));
  Comparator #(.width(5)) comparator_1 (.a(wsbh), .b(5'b00010), .eq(comparator_1_eq));  // open: gt, lt
  funct funct_1 (
    .funct(funct), .addu(funct_1_addu), .subu(funct_1_subu), .jr(funct_1_jr), .jalr(funct_1_jalr),
    .sll(funct_1_sll), .wsbh(funct_1_wsbh));
  and subu (subu_out, opcode_1_subu, funct_1_subu);
  and addu (addu_out, opcode_1_addu, funct_1_addu);
  buf ori (ori_out, opcode_1_ori);  // AND_Gate
  buf lw (lw_out, opcode_1_lw);  // AND_Gate
  buf sw (sw_out, opcode_1_sw);  // AND_Gate
  buf beq (beq_out, opcode_1_beq);  // AND_Gate
  buf lui (lui_out, opcode_1_lui);  // AND_Gate
  buf jal (jal_out, opcode_1_jal);  // AND_Gate
  and jalr (jalr_out, opcode_1_jalr, funct_1_jalr);
  and jr (jr_out, opcode_1_jr, funct_1_jr);
  buf lb (lb_out, opcode_1_lb);  // AND_Gate
  buf lh (lh_out, opcode_1_lh);  // AND_Gate
  buf sh (sh_out, opcode_1_sh);  // AND_Gate
  buf sb (sb_out, opcode_1_sb);  // AND_Gate
  and sll (sll_out, opcode_1_sll, funct_1_sll);
  buf balr (balr_out, opcode_1_balr);  // AND_Gate
  and u_wsbh (wsbh_out, opcode_1_wsbh, comparator_1_eq, funct_1_wsbh);
  buf lbi (lbi_out, opcode_1_lbi);  // AND_Gate
  or u_RegDst (RegDst_out, ori_out, lw_out, sw_out, lui_out, lb_out, lh_out, balr_out, lbi_out);
  or RegDst_2 (RegDst_2_out, addu_out, subu_out, sll_out, jalr_out, wsbh_out);
  buf RegDst_3 (RegDst_3_out, jal_out);  // OR_Gate
  or u_AluSrc (AluSrc, ori_out, lw_out, lui_out, sw_out, lb_out, lh_out, sb_out, sh_out, balr_out, lbi_out);
  or u_RegWrite (RegWrite, addu_out, subu_out, lui_out, ori_out, lw_out, jal_out, jalr_out, lb_out, lh_out, sll_out, balr_out, wsbh_out, lbi_out);
  or u_MemToReg (MemToReg, lw_out, lb_out, lh_out, lbi_out);
  or u_MemWrite (MemWrite, sw_out, sb_out, sh_out);
  or bgt (Branch[0], balr_out, 1'b0);
  or beq_2 (Branch[1], beq_out, balr_out);
  or blt (Branch[2], balr_out, 1'b0);
  or u_Jump (Jump, jal_out, jr_out, jalr_out, 1'b0);
  or u_Link (Link, jal_out, jalr_out, balr_out, 1'b0);
  or u_Return (Return, jr_out, jalr_out, 1'b0);
  or u_Byte (Byte, lb_out, sb_out, lbi_out, 1'b0);
  or u_Half (Half, lh_out, sh_out, 1'b0);
  or u_Sign (Sign, lb_out, lh_out, 1'b0);
  buf u_ByteCat (ByteCat, lbi_out);  // OR_Gate
  or add (add_out, addu_out, lw_out, sw_out, lui_out, lb_out, lh_out, sb_out, sh_out, balr_out, lbi_out, 1'b0);
  or sub (sub_out, subu_out, 1'b0);
  or sll_2 (sll_2_out, sll_out, 1'b0);
  buf srl (srl_out, 1'b0);  // OR_Gate
  buf sra (sra_out, 1'b0);  // OR_Gate
  buf \and  (and_out, 1'b0);  // OR_Gate
  or \or  (or_out, ori_out, 1'b0);
  buf \xor  (xor_out, 1'b0);  // OR_Gate
  or compu (compu_out, beq_out, 1'b0);
  buf comp (comp_out, 1'b0);  // OR_Gate
  or swap (swap_out, wsbh_out, 1'b0);
  or Ext_Zero (Ext_Zero_out, ori_out, 1'b0);
  or Ext_Sign (Ext_Sign_out, lw_out, sw_out, beq_out, lb_out, lh_out, sb_out, sh_out, balr_out, lbi_out, 1'b0);
  or Ext_Up (Ext_Up_out, lui_out, 1'b0);
  or Ext_26 (Ext_26_out, jal_out, 1'b0);
  Priority_Encoder #(.select(2)) priority_encoder_1 (
    .in0(RegDst_out), .in1(RegDst_2_out), .in2(RegDst_3_out), .out(RegDst));  // open: in3, gs, en_out, en_in
  Pull_Resistor pull_resistor_1 (.node(RegDst));
  Priority_Encoder #(.select(4)) priority_encoder_2 (
    .in0(add_out), .in1(sub_out), .in2(sll_2_out), .in3(srl_out), .in4(sra_out), .in5(and_out), .in6(or_out),
    .in7(xor_out), .in8(compu_out), .in9(comp_out), .in10(swap_out), .out(AluCtrl));  // open: in11, in12, in13, in14, in15, gs, en_out, en_in
  Priority_Encoder #(.select(2)) priority_encoder_3 (
    .in0(Ext_Zero_out), .in1(Ext_Sign_out), .in2(Ext_Up_out), .in3(Ext_26_out), .out(ExtCtrl));  // open: gs, en_out, en_in
  Pull_Resistor pull_resistor_2 (.node(ExtCtrl));
  Pull_Resistor pull_resistor_3 (.node(AluCtrl));
endmodule

module opcode (
  input  [5:0] opcode,
  output addu,
  output subu,
  output ori,
  output lw,
  output sw,
  output beq,
  output lui,
  output jal,
  output jr,
  output jalr,
  output lb,
  output lh,
  output sb,
  output sh,
  output sll,
  output balr,
  output wsbh,
  output lbi
);

  and u_addu (addu, ~opcode[0], ~opcode[1], ~opcode[2], ~opcode[3], ~opcode[4], ~opcode[5]);  // AND_Gate
  and u_subu (subu, ~opcode[0], ~opcode[1], ~opcode[2], ~opcode[3], ~opcode[4], ~opcode[5]);  // AND_Gate
  and u_ori (ori, opcode[0], ~opcode[1], opcode[2], opcode[3], ~opcode[4], ~opcode[5]);  // AND_Gate
  and u_lw (lw, opcode[0], opcode[1], ~opcode[2], ~opcode[3], ~opcode[4], opcode[5]);  // AND_Gate
  and u_sw (sw, opcode[0], opcode[1], ~opcode[2], opcode[3], ~opcode[4], opcode[5]);  // AND_Gate
  and u_beq (beq, ~opcode[0], ~opcode[1], opcode[2], ~opcode[3], ~opcode[4], ~opcode[5]);  // AND_Gate
  and u_lui (lui, opcode[0], opcode[1], opcode[2], opcode[3], ~opcode[4], ~opcode[5]);  // AND_Gate
  and u_jal (jal, opcode[0], opcode[1], ~opcode[2], ~opcode[3], ~opcode[4], ~opcode[5]);  // AND_Gate
  and u_jr (jr, ~opcode[0], ~opcode[1], ~opcode[2], ~opcode[3], ~opcode[4], ~opcode[5]);  // AND_Gate
  and u_jalr (jalr, ~opcode[0], ~opcode[1], ~opcode[2], ~opcode[3], ~opcode[4], ~opcode[5]);  // AND_Gate
  and u_lb (lb, ~opcode[0], ~opcode[1], ~opcode[2], ~opcode[3], ~opcode[4], opcode[5]);  // AND_Gate
  and u_lh (lh, opcode[0], ~opcode[1], ~opcode[2], ~opcode[3], ~opcode[4], opcode[5]);  // AND_Gate
  and u_sb (sb, ~opcode[0], ~opcode[1], ~opcode[2], opcode[3], ~opcode[4], opcode[5]);  // AND_Gate
  and u_sh (sh, opcode[0], ~opcode[1], ~opcode[2], opcode[3], ~opcode[4], opcode[5]);  // AND_Gate
  and u_sll (sll, ~opcode[0], ~opcode[1], ~opcode[2], ~opcode[3], ~opcode[4], ~opcode[5]);  // AND_Gate
  and u_balr (balr, ~opcode[0], opcode[1], opcode[2], ~opcode[3], opcode[4], opcode[5]);  // AND_Gate
  and u_wsbh (wsbh, opcode[0], opcode[1], opcode[2], opcode[3], opcode[4], ~opcode[5]);  // AND_Gate
  and u_lbi (lbi, opcode[0], ~opcode[1], opcode[2], opcode[3], opcode[4], opcode[5]);  // AND_Gate
endmodule

module funct (
  input  [5:0] funct,
  output addu,
  output subu,
  output jr,
  output jalr,
  output sll,
  output wsbh
);

  and u_addu (addu, funct[0], ~funct[1], ~funct[2], ~funct[3], ~funct[4], funct[5]);  // AND_Gate
  and u_subu (subu, funct[0], funct[1], ~funct[2], ~funct[3], ~funct[4], funct[5]);  // AND_Gate
  and u_jr (jr, ~funct[0], ~funct[1], ~funct[2], funct[3], ~funct[4], ~funct[5]);  // AND_Gate
  and u_jalr (jalr, funct[0], ~funct[1], ~funct[2], funct[3], ~funct[4], ~funct[5]);  // AND_Gate
  and u_sll (sll, ~funct[0], ~funct[1], ~funct[2], ~funct[3], ~funct[4], ~funct[5]);  // AND_Gate
  and u_wsbh (wsbh, ~funct[0], ~funct[1], ~funct[2], ~funct[3], ~funct[4], funct[5]);  // AND_Gate
endmodule

module StoreType (
  input  Byte,
  input  Half,
  input  [31:0] RegData,
  input  [1:0] offset,
  input  [31:0] MemData,
  output [31:0] out_6
);

  wire bitselector_1_out, decoder_1_out0, decoder_1_out1, decoder_1_out2, decoder_1_out3, decoder_2_out0,
       decoder_2_out1;
  wire [7:0] multiplexer_1_out, multiplexer_2_out, multiplexer_3_out, multiplexer_4_out;
  wire [15:0] multiplexer_5_out, multiplexer_6_out;
  wire [31:0] multiplexer_7_out;

  Decoder #(.select(2), .enable("false")) decoder_1 (
    .out0(decoder_1_out0), .out1(decoder_1_out1), .out2(decoder_1_out2), .out3(decoder_1_out3), .sel(offset));
  BitSelector #(.width(2)) bitselector_1 (.in(offset), .out(bitselector_1_out), .sel(1'b1));
  Decoder #(.enable("false")) decoder_2 (.out0(decoder_2_out0), .out1(decoder_2_out1), .sel(bitselector_1_out));
  Multiplexer #(.width(8), .enable("false")) multiplexer_1 (
    .in0(MemData[7:0]), .in1(RegData[7:0]), .out(multiplexer_1_out), .sel(decoder_1_out0));
  Multiplexer #(.width(8), .enable("false")) multiplexer_2 (
    .in0(MemData[15:8]), .in1(RegData[7:0]), .out(multiplexer_2_out), .sel(decoder_1_out1));
  Multiplexer #(.width(8), .enable("false")) multiplexer_3 (
    .in0(MemData[23:16]), .in1(RegData[7:0]), .out(multiplexer_3_out), .sel(decoder_1_out2));
  Multiplexer #(.width(8), .enable("false")) multiplexer_4 (
    .in0(MemData[31:24]), .in1(RegData[7:0]), .out(multiplexer_4_out), .sel(decoder_1_out3));
  Multiplexer #(.width(16), .enable("false")) multiplexer_5 (
    .in0(MemData[15:0]), .in1(RegData[15:0]), .out(multiplexer_5_out), .sel(decoder_2_out0));
  Multiplexer #(.width(16), .enable("false")) multiplexer_6 (
    .in0(MemData[31:16]), .in1(RegData[15:0]), .out(multiplexer_6_out), .sel(decoder_2_out1));
  Multiplexer #(.width(32), .enable("false")) multiplexer_7 (
    .in0(RegData), .in1({multiplexer_4_out, multiplexer_3_out, multiplexer_2_out, multiplexer_1_out}),
    .out(multiplexer_7_out), .sel(Byte));
  Multiplexer #(.width(32), .enable("false")) multiplexer_8 (
    .in0(multiplexer_7_out), .in1({multiplexer_6_out, multiplexer_5_out}), .out(out_6), .sel(Half));

  // Other names for the same wires on the sheet: Mem_7_0[7:0] = MemData[7:0]; Mem_15_0[15:0] = MemData[15:0];
  //   Mem_15_8[7:0] = MemData[15:8]; Mem_23_16[7:0] = MemData[23:16]; Mem_31_16[15:0] = MemData[31:16];
  //   Mem_31_24[7:0] = MemData[31:24]; Reg_7_0[7:0] = RegData[7:0]; Reg_15_0[15:0] = RegData[15:0];
  //   Reg_15_8[7:0] = RegData[15:8]; Reg_23_16[7:0] = RegData[23:16]; Reg_31_16[15:0] = RegData[31:16];
  //   Reg_31_24[7:0] = RegData[31:24]
endmodule

module LoadType (
  input  Byte,
  input  Half,
  input  [31:0] RegData,
  input  [1:0] offset,
  input  [31:0] MemData,
  output [31:0] out_6
);

  wire bitselector_1_out, decoder_1_out0, decoder_1_out1, decoder_1_out2, decoder_1_out3, decoder_2_out0,
       decoder_2_out1;
  wire [7:0] multiplexer_1_out, multiplexer_2_out, multiplexer_3_out, multiplexer_4_out;
  wire [15:0] multiplexer_5_out, multiplexer_6_out;
  wire [31:0] multiplexer_7_out;

  Decoder #(.select(2), .enable("false")) decoder_1 (
    .out0(decoder_1_out0), .out1(decoder_1_out1), .out2(decoder_1_out2), .out3(decoder_1_out3), .sel(offset));
  BitSelector #(.width(2)) bitselector_1 (.in(offset), .out(bitselector_1_out), .sel(1'b1));
  Decoder #(.enable("false")) decoder_2 (.out0(decoder_2_out0), .out1(decoder_2_out1), .sel(bitselector_1_out));
  Multiplexer #(.width(8), .enable("false")) multiplexer_1 (
    .in0(MemData[7:0]), .in1(RegData[7:0]), .out(multiplexer_1_out), .sel(decoder_1_out0));
  Multiplexer #(.width(8), .enable("false")) multiplexer_2 (
    .in0(MemData[15:8]), .in1(RegData[15:8]), .out(multiplexer_2_out), .sel(decoder_1_out1));
  Multiplexer #(.width(8), .enable("false")) multiplexer_3 (
    .in0(MemData[23:16]), .in1(RegData[23:16]), .out(multiplexer_3_out), .sel(decoder_1_out2));
  Multiplexer #(.width(8), .enable("false")) multiplexer_4 (
    .in0(MemData[31:24]), .in1(RegData[31:24]), .out(multiplexer_4_out), .sel(decoder_1_out3));
  Multiplexer #(.width(16), .enable("false")) multiplexer_5 (
    .in0(MemData[15:0]), .in1(RegData[15:0]), .out(multiplexer_5_out), .sel(decoder_2_out0));
  Multiplexer #(.width(16), .enable("false")) multiplexer_6 (
    .in0(MemData[31:16]), .in1(RegData[15:0]), .out(multiplexer_6_out), .sel(decoder_2_out1));
  Multiplexer #(.width(32), .enable("false")) multiplexer_7 (
    .in0(RegData), .in1({multiplexer_4_out, multiplexer_3_out, multiplexer_2_out, multiplexer_1_out}),
    .out(multiplexer_7_out), .sel(Byte));
  Multiplexer #(.width(32), .enable("false")) multiplexer_8 (
    .in0(multiplexer_7_out), .in1({multiplexer_6_out, multiplexer_5_out}), .out(out_6), .sel(Half));

  // Other names for the same wires on the sheet: Mem_7_0[7:0] = MemData[7:0]; Mem_15_0[15:0] = MemData[15:0];
  //   Mem_15_8[7:0] = MemData[15:8]; Mem_23_16[7:0] = MemData[23:16]; Mem_31_16[15:0] = MemData[31:16];
  //   Mem_31_24[7:0] = MemData[31:24]; Reg_7_0[7:0] = RegData[7:0]; Reg_15_0[15:0] = RegData[15:0];
  //   Reg_15_8[7:0] = RegData[15:8]; Reg_23_16[7:0] = RegData[23:16]; Reg_31_16[15:0] = RegData[31:16];
  //   Reg_31_24[7:0] = RegData[31:24]
endmodule
