// Logisim project conversion.circ as structural Verilog: 5 circuits, main circuit main
module main (
  input  [8:0] in,
  input  [1:0] op,
  output [3:0] out1,
  output [3:0] out2,
  output [3:0] out3
);

  conversion conversion_1 (.in(in), .op(op), .out1(out1), .out2(out2), .out3(out3));
endmodule

module _2to10 (
  input  [8:0] in,
  output [3:0] out1,
  output [3:0] out2,
  output [3:0] out3
);

  wire [8:0] divider_1_rem, divider_2_out, divider_3_out, divider_4_rem;

  Divider #(.width(9)) divider_1 (.a(in), .b(9'ha), .rem(divider_1_rem));  // open: out, upper
  Divider #(.width(9)) divider_2 (.a(in), .b(9'ha), .out(divider_2_out));  // open: upper, rem
  Divider #(.width(9)) divider_3 (.a(in), .b(9'h64), .out(divider_3_out));  // open: upper, rem
  Bit_Extender #(.in_width(9), .out_width(4)) bit_extender_1 (.in(divider_3_out), .out(out3));
  Bit_Extender #(.in_width(9), .out_width(4)) bit_extender_2 (.in(divider_1_rem), .out(out1));
  Divider #(.width(9)) divider_4 (.a(divider_2_out), .b(9'ha), .rem(divider_4_rem));  // open: out, upper
  Bit_Extender #(.in_width(9), .out_width(4)) bit_extender_3 (.in(divider_4_rem), .out(out2));
endmodule

module _2to8 (
  input  [8:0] in,
  output [3:0] out1,
  output [3:0] out2,
  output [3:0] out3
);

  assign out1 = {{1{1'b0}}, in[2:0]};  // Bit_Extender bit_extender_1
  assign out2 = {{1{1'b0}}, in[5:3]};  // Bit_Extender bit_extender_2
  assign out3 = {{1{1'b0}}, in[8:6]};  // Bit_Extender bit_extender_3
endmodule

module _2to16 (
  input  [8:0] in,
  output [3:0] out1,
  output [3:0] out2,
  output [3:0] out3
);

  assign out3 = {{3{1'b0}}, in[8]};  // Bit_Extender bit_extender_1

  assign out1 = in[3:0];
  assign out2 = in[7:4];
endmodule

module conversion (
  input  [8:0] in,
  input  [1:0] op,
  output [3:0] out1,
  output [3:0] out2,
  output [3:0] out3
);

  wire [3:0] n2to8_1_out1, n2to8_1_out2, n2to8_1_out3, n2to10_1_out1, n2to10_1_out2, n2to10_1_out3,
       n2to16_1_out1, n2to16_1_out2, n2to16_1_out3;

  _2to8 u_2to8_1 (.in(in), .out1(n2to8_1_out1), .out2(n2to8_1_out2), .out3(n2to8_1_out3));
  _2to10 u_2to10_1 (.in(in), .out1(n2to10_1_out1), .out2(n2to10_1_out2), .out3(n2to10_1_out3));
  _2to16 u_2to16_1 (.in(in), .out1(n2to16_1_out1), .out2(n2to16_1_out2), .out3(n2to16_1_out3));
  Multiplexer #(.select(2), .width(4), .enable("false")) multiplexer_1 (
    .in0(n2to8_1_out1), .in1(n2to10_1_out1), .in2(n2to16_1_out1), .out(out1), .sel(op));  // open: in3
  Multiplexer #(.select(2), .width(4), .enable("false")) multiplexer_2 (
    .in0(n2to8_1_out2), .in1(n2to10_1_out2), .in2(n2to16_1_out2), .out(out2), .sel(op));  // open: in3
  Multiplexer #(.select(2), .width(4), .enable("false")) multiplexer_3 (
    .in0(n2to8_1_out3), .in1(n2to10_1_out3), .in2(n2to16_1_out3), .out(out3), .sel(op));  // open: in3
endmodule
